// Digital circuit A_shift_B_R32b.dig as structural Verilog
module A_shift_B_R32b (
  input  [31:0] A,
  input  [31:0] B,
  output [31:0] S
);

  wire [31:0] r_shifter_32b_1_s, r_shifter_32b_2_s, r_shifter_32b_3_s, r_shifter_32b_4_s, r_shifter_32b_5_s,
       r_shifter_32b_6_s, r_shifter_32b_7_s, r_shifter_32b_8_s, r_shifter_32b_9_s, r_shifter_32b_10_s,
       r_shifter_32b_11_s, r_shifter_32b_12_s, r_shifter_32b_13_s, r_shifter_32b_14_s, r_shifter_32b_15_s,
       r_shifter_32b_16_s, r_shifter_32b_17_s, r_shifter_32b_18_s, r_shifter_32b_19_s, r_shifter_32b_20_s,
       r_shifter_32b_21_s, r_shifter_32b_22_s, r_shifter_32b_23_s, r_shifter_32b_24_s, r_shifter_32b_25_s,
       r_shifter_32b_26_s, r_shifter_32b_27_s, r_shifter_32b_28_s, r_shifter_32b_29_s, r_shifter_32b_30_s,
       r_shifter_32b_31_s;

  R_Shifter_32b r_shifter_32b_1 (.A(A), .S(r_shifter_32b_1_s));
  R_Shifter_32b r_shifter_32b_2 (.A(r_shifter_32b_1_s), .S(r_shifter_32b_2_s));
  R_Shifter_32b r_shifter_32b_3 (.A(r_shifter_32b_2_s), .S(r_shifter_32b_3_s));
  R_Shifter_32b r_shifter_32b_4 (.A(r_shifter_32b_3_s), .S(r_shifter_32b_4_s));
  R_Shifter_32b r_shifter_32b_5 (.A(r_shifter_32b_4_s), .S(r_shifter_32b_5_s));
  R_Shifter_32b r_shifter_32b_6 (.A(r_shifter_32b_5_s), .S(r_shifter_32b_6_s));
  R_Shifter_32b r_shifter_32b_7 (.A(r_shifter_32b_6_s), .S(r_shifter_32b_7_s));
  R_Shifter_32b r_shifter_32b_8 (.A(r_shifter_32b_7_s), .S(r_shifter_32b_8_s));
  R_Shifter_32b r_shifter_32b_9 (.A(r_shifter_32b_8_s), .S(r_shifter_32b_9_s));
  R_Shifter_32b r_shifter_32b_10 (.A(r_shifter_32b_9_s), .S(r_shifter_32b_10_s));
  R_Shifter_32b r_shifter_32b_11 (.A(r_shifter_32b_10_s), .S(r_shifter_32b_11_s));
  R_Shifter_32b r_shifter_32b_12 (.A(r_shifter_32b_11_s), .S(r_shifter_32b_12_s));
  R_Shifter_32b r_shifter_32b_13 (.A(r_shifter_32b_12_s), .S(r_shifter_32b_13_s));
  R_Shifter_32b r_shifter_32b_14 (.A(r_shifter_32b_13_s), .S(r_shifter_32b_14_s));
  R_Shifter_32b r_shifter_32b_15 (.A(r_shifter_32b_14_s), .S(r_shifter_32b_15_s));
  R_Shifter_32b r_shifter_32b_16 (.A(r_shifter_32b_15_s), .S(r_shifter_32b_16_s));
  R_Shifter_32b r_shifter_32b_17 (.A(r_shifter_32b_16_s), .S(r_shifter_32b_17_s));
  R_Shifter_32b r_shifter_32b_18 (.A(r_shifter_32b_17_s), .S(r_shifter_32b_18_s));
  R_Shifter_32b r_shifter_32b_19 (.A(r_shifter_32b_18_s), .S(r_shifter_32b_19_s));
  R_Shifter_32b r_shifter_32b_20 (.A(r_shifter_32b_19_s), .S(r_shifter_32b_20_s));
  R_Shifter_32b r_shifter_32b_21 (.A(r_shifter_32b_20_s), .S(r_shifter_32b_21_s));
  R_Shifter_32b r_shifter_32b_22 (.A(r_shifter_32b_21_s), .S(r_shifter_32b_22_s));
  R_Shifter_32b r_shifter_32b_23 (.A(r_shifter_32b_22_s), .S(r_shifter_32b_23_s));
  R_Shifter_32b r_shifter_32b_24 (.A(r_shifter_32b_23_s), .S(r_shifter_32b_24_s));
  R_Shifter_32b r_shifter_32b_25 (.A(r_shifter_32b_24_s), .S(r_shifter_32b_25_s));
  R_Shifter_32b r_shifter_32b_26 (.A(r_shifter_32b_25_s), .S(r_shifter_32b_26_s));
  R_Shifter_32b r_shifter_32b_27 (.A(r_shifter_32b_26_s), .S(r_shifter_32b_27_s));
  R_Shifter_32b r_shifter_32b_28 (.A(r_shifter_32b_27_s), .S(r_shifter_32b_28_s));
  R_Shifter_32b r_shifter_32b_29 (.A(r_shifter_32b_28_s), .S(r_shifter_32b_29_s));
  R_Shifter_32b r_shifter_32b_30 (.A(r_shifter_32b_29_s), .S(r_shifter_32b_30_s));
  R_Shifter_32b r_shifter_32b_31 (.A(r_shifter_32b_30_s), .S(r_shifter_32b_31_s));
  Multiplexer #(.Selector_Bits(5), .Bits(32)) multiplexer_1 (
    .sel(B[4:0]), .in_0(A), .in_1(r_shifter_32b_1_s), .in_2(r_shifter_32b_2_s), .in_3(r_shifter_32b_3_s),
    .in_4(r_shifter_32b_4_s), .in_5(r_shifter_32b_5_s), .in_6(r_shifter_32b_6_s), .in_7(r_shifter_32b_7_s),
    .in_8(r_shifter_32b_8_s), .in_9(r_shifter_32b_9_s), .in_10(r_shifter_32b_10_s),
    .in_11(r_shifter_32b_11_s), .in_12(r_shifter_32b_12_s), .in_13(r_shifter_32b_13_s),
    .in_14(r_shifter_32b_14_s), .in_15(r_shifter_32b_15_s), .in_16(r_shifter_32b_16_s),
    .in_17(r_shifter_32b_17_s), .in_18(r_shifter_32b_18_s), .in_19(r_shifter_32b_19_s),
    .in_20(r_shifter_32b_20_s), .in_21(r_shifter_32b_21_s), .in_22(r_shifter_32b_22_s),
    .in_23(r_shifter_32b_23_s), .in_24(r_shifter_32b_24_s), .in_25(r_shifter_32b_25_s),
    .in_26(r_shifter_32b_26_s), .in_27(r_shifter_32b_27_s), .in_28(r_shifter_32b_28_s),
    .in_29(r_shifter_32b_29_s), .in_30(r_shifter_32b_30_s), .in_31(r_shifter_32b_31_s), .out(S));
endmodule
