// Digital circuit Banco_de_Registradores_16R.dig as structural Verilog
module Banco_de_Registradores_16R (
  input  We,
  input  [3:0] End__Rc,
  input  CLK,
  input  [31:0] D,
  input  [3:0] End__Ra,
  input  [3:0] End__Rb,
  output [31:0] R_a,
  output [31:0] R_b
);

  wire demultiplexer_1_out_0, demultiplexer_1_out_1, demultiplexer_1_out_2, demultiplexer_1_out_3,
       demultiplexer_1_out_4, demultiplexer_1_out_5, demultiplexer_1_out_6, demultiplexer_1_out_7,
       demultiplexer_1_out_8, demultiplexer_1_out_9, demultiplexer_1_out_10, demultiplexer_1_out_11,
       demultiplexer_1_out_12, demultiplexer_1_out_13, demultiplexer_1_out_14, demultiplexer_1_out_15;
  wire [31:0] multiplexer_1_out, multiplexer_2_out, multiplexer_3_out, multiplexer_4_out, multiplexer_5_out,
       multiplexer_6_out, multiplexer_7_out, multiplexer_8_out, multiplexer_9_out, multiplexer_10_out,
       multiplexer_11_out, multiplexer_12_out, multiplexer_13_out, multiplexer_14_out, multiplexer_15_out,
       multiplexer_16_out, reg_32b_1_q, reg_32b_2_q, reg_32b_3_q, reg_32b_4_q, reg_32b_5_q, reg_32b_6_q,
       reg_32b_7_q, reg_32b_8_q, reg_32b_9_q, reg_32b_10_q, reg_32b_11_q, reg_32b_12_q, reg_32b_13_q,
       reg_32b_14_q, reg_32b_15_q, reg_32b_16_q;

  Demultiplexer #(.Selector_Bits(4)) demultiplexer_1 (
    .sel(End__Rc), .in(We), .out_0(demultiplexer_1_out_0), .out_1(demultiplexer_1_out_1),
    .out_2(demultiplexer_1_out_2), .out_3(demultiplexer_1_out_3), .out_4(demultiplexer_1_out_4),
    .out_5(demultiplexer_1_out_5), .out_6(demultiplexer_1_out_6), .out_7(demultiplexer_1_out_7),
    .out_8(demultiplexer_1_out_8), .out_9(demultiplexer_1_out_9), .out_10(demultiplexer_1_out_10),
    .out_11(demultiplexer_1_out_11), .out_12(demultiplexer_1_out_12), .out_13(demultiplexer_1_out_13),
    .out_14(demultiplexer_1_out_14), .out_15(demultiplexer_1_out_15));
  Multiplexer #(.Bits(32)) multiplexer_1 (
    .sel(demultiplexer_1_out_0), .in_0(reg_32b_1_q), .in_1(reg_32b_1_q), .out(multiplexer_1_out));
  Multiplexer #(.Bits(32)) multiplexer_2 (
    .sel(demultiplexer_1_out_1), .in_0(reg_32b_2_q), .in_1(D), .out(multiplexer_2_out));
  Multiplexer #(.Bits(32)) multiplexer_3 (
    .sel(demultiplexer_1_out_2), .in_0(reg_32b_3_q), .in_1(D), .out(multiplexer_3_out));
  Multiplexer #(.Bits(32)) multiplexer_4 (
    .sel(demultiplexer_1_out_3), .in_0(reg_32b_4_q), .in_1(D), .out(multiplexer_4_out));
  Multiplexer #(.Bits(32)) multiplexer_5 (
    .sel(demultiplexer_1_out_4), .in_0(reg_32b_5_q), .in_1(D), .out(multiplexer_5_out));
  Multiplexer #(.Bits(32)) multiplexer_6 (
    .sel(demultiplexer_1_out_5), .in_0(reg_32b_6_q), .in_1(D), .out(multiplexer_6_out));
  Multiplexer #(.Bits(32)) multiplexer_7 (
    .sel(demultiplexer_1_out_6), .in_0(reg_32b_7_q), .in_1(D), .out(multiplexer_7_out));
  Multiplexer #(.Bits(32)) multiplexer_8 (
    .sel(demultiplexer_1_out_7), .in_0(reg_32b_8_q), .in_1(D), .out(multiplexer_8_out));
  Multiplexer #(.Bits(32)) multiplexer_9 (
    .sel(demultiplexer_1_out_8), .in_0(reg_32b_9_q), .in_1(D), .out(multiplexer_9_out));
  Multiplexer #(.Bits(32)) multiplexer_10 (
    .sel(demultiplexer_1_out_9), .in_0(reg_32b_10_q), .in_1(D), .out(multiplexer_10_out));
  Multiplexer #(.Bits(32)) multiplexer_11 (
    .sel(demultiplexer_1_out_10), .in_0(reg_32b_11_q), .in_1(D), .out(multiplexer_11_out));
  Multiplexer #(.Bits(32)) multiplexer_12 (
    .sel(demultiplexer_1_out_11), .in_0(reg_32b_12_q), .in_1(D), .out(multiplexer_12_out));
  Multiplexer #(.Bits(32)) multiplexer_13 (
    .sel(demultiplexer_1_out_12), .in_0(reg_32b_13_q), .in_1(D), .out(multiplexer_13_out));
  Multiplexer #(.Bits(32)) multiplexer_14 (
    .sel(demultiplexer_1_out_13), .in_0(reg_32b_14_q), .in_1(D), .out(multiplexer_14_out));
  Multiplexer #(.Bits(32)) multiplexer_15 (
    .sel(demultiplexer_1_out_14), .in_0(reg_32b_15_q), .in_1(D), .out(multiplexer_15_out));
  Multiplexer #(.Bits(32)) multiplexer_16 (
    .sel(demultiplexer_1_out_15), .in_0(reg_32b_16_q), .in_1(D), .out(multiplexer_16_out));
  Reg_32b reg_32b_1 (.D(multiplexer_1_out), .CLK(CLK), .Q(reg_32b_1_q));
  Reg_32b reg_32b_2 (.D(multiplexer_2_out), .CLK(CLK), .Q(reg_32b_2_q));
  Reg_32b reg_32b_3 (.D(multiplexer_3_out), .CLK(CLK), .Q(reg_32b_3_q));
  Reg_32b reg_32b_4 (.D(multiplexer_4_out), .CLK(CLK), .Q(reg_32b_4_q));
  Reg_32b reg_32b_5 (.D(multiplexer_5_out), .CLK(CLK), .Q(reg_32b_5_q));
  Reg_32b reg_32b_6 (.D(multiplexer_6_out), .CLK(CLK), .Q(reg_32b_6_q));
  Reg_32b reg_32b_7 (.D(multiplexer_7_out), .CLK(CLK), .Q(reg_32b_7_q));
  Reg_32b reg_32b_8 (.D(multiplexer_8_out), .CLK(CLK), .Q(reg_32b_8_q));
  Reg_32b reg_32b_9 (.D(multiplexer_9_out), .CLK(CLK), .Q(reg_32b_9_q));
  Reg_32b reg_32b_10 (.D(multiplexer_10_out), .CLK(CLK), .Q(reg_32b_10_q));
  Reg_32b reg_32b_11 (.D(multiplexer_11_out), .CLK(CLK), .Q(reg_32b_11_q));
  Reg_32b reg_32b_12 (.D(multiplexer_12_out), .CLK(CLK), .Q(reg_32b_12_q));
  Reg_32b reg_32b_13 (.D(multiplexer_13_out), .CLK(CLK), .Q(reg_32b_13_q));
  Reg_32b reg_32b_14 (.D(multiplexer_14_out), .CLK(CLK), .Q(reg_32b_14_q));
  Reg_32b reg_32b_15 (.D(multiplexer_15_out), .CLK(CLK), .Q(reg_32b_15_q));
  Reg_32b reg_32b_16 (.D(multiplexer_16_out), .CLK(CLK), .Q(reg_32b_16_q));
  Multiplexer #(.Selector_Bits(4), .Bits(32)) multiplexer_17 (
    .sel(End__Ra), .in_0(reg_32b_1_q), .in_1(reg_32b_2_q), .in_2(reg_32b_3_q), .in_3(reg_32b_4_q),
    .in_4(reg_32b_5_q), .in_5(reg_32b_6_q), .in_6(reg_32b_7_q), .in_7(reg_32b_8_q), .in_8(reg_32b_9_q),
    .in_9(reg_32b_10_q), .in_10(reg_32b_11_q), .in_11(reg_32b_12_q), .in_12(reg_32b_13_q),
    .in_13(reg_32b_14_q), .in_14(reg_32b_15_q), .in_15(reg_32b_16_q), .out(R_a));
  Multiplexer #(.Selector_Bits(4), .Bits(32)) multiplexer_18 (
    .sel(End__Rb), .in_0(reg_32b_1_q), .in_1(reg_32b_2_q), .in_2(reg_32b_3_q), .in_3(reg_32b_4_q),
    .in_4(reg_32b_5_q), .in_5(reg_32b_6_q), .in_6(reg_32b_7_q), .in_7(reg_32b_8_q), .in_8(reg_32b_9_q),
    .in_9(reg_32b_10_q), .in_10(reg_32b_11_q), .in_11(reg_32b_12_q), .in_12(reg_32b_13_q),
    .in_13(reg_32b_14_q), .in_14(reg_32b_15_q), .in_15(reg_32b_16_q), .out(R_b));
endmodule
