// Digital circuit Extensor_16_32.dig as structural Verilog
module Extensor_16_32 (
  input  [15:0] A,
  output [31:0] S
);

  _1P16 _1p16_1 (.A(A[15]), .S(S[31:16]));

  assign S[15:0] = A;
endmodule
