// Digital circuit FullAdder_Prop_Ger.dig as structural Verilog
module FullAdder_Prop_Ger (
  input  Cin,
  input  A,
  input  B,
  output S,
  output Pi,
  output Gi
);

  FullAdder fulladder_1 (.A(A), .B(B), .Cin(Cin), .S(S));  // open: Cout
  Gi_Pi gi_pi_1 (.Ai(A), .Bi(B), .Gi(Gi), .Pi(Pi));
endmodule
