// Digital circuit MicoX1.dig as structural Verilog
module MicoX1 (
  input  clk,
  output [31:0] Display
);

  wire ula_2_0_1_zero;
  wire [7:0] Mem__Controle_d;
  wire [23:0] ext24bits_1_s, ext24bits_2_s, IP_q, multiplexer_1_out, multiplexer_3_out, multiplexer_4_out,
       somador_24b_1_s;
  wire [31:0] banco_de_registradores_16r_1_r_a, banco_de_registradores_16r_1_r_b, extensor_16_32_1_s,
       \Mem__Instruções_d , multiplexer_2_out, ula_2_0_1_s;

  Multiplexer #(.Bits(24)) multiplexer_1 (
    .sel(Mem__Controle_d[1]), .in_0(multiplexer_4_out), .in_1(ext24bits_1_s), .out(multiplexer_1_out));
  Somador_24b somador_24b_1 (.A(IP_q), .B(multiplexer_1_out), .Cin(1'b0), .S(somador_24b_1_s));
  D_FF #(.Bits(24)) IP (.D(somador_24b_1_s), .C(clk), .Q(IP_q));  // open: nQ
  ROM #(.AddrBits(24), .Bits(32)) \Mem__Instruções  (.A(IP_q), .sel(1'b1), .D(\Mem__Instruções_d ));
  Ext24bits ext24bits_1 (.A(\Mem__Instruções_d [15:0]), .S(ext24bits_1_s));
  ROM #(.AddrBits(4), .Bits(8)) Mem__Controle (.A(\Mem__Instruções_d [31:28]), .sel(1'b1), .D(Mem__Controle_d));
  Ext24bits ext24bits_2 (.A(\Mem__Instruções_d [15:0]), .S(ext24bits_2_s));
  Banco_de_Registradores_16R banco_de_registradores_16r_1 (
    .We(Mem__Controle_d[3]), .End__Rc(\Mem__Instruções_d [19:16]), .CLK(clk), .D(ula_2_0_1_s),
    .End__Ra(\Mem__Instruções_d [27:24]), .End__Rb(\Mem__Instruções_d [23:20]),
    .R_a(banco_de_registradores_16r_1_r_a), .R_b(banco_de_registradores_16r_1_r_b));
  Extensor_16_32 extensor_16_32_1 (.A(\Mem__Instruções_d [15:0]), .S(extensor_16_32_1_s));
  Multiplexer #(.Bits(32)) multiplexer_2 (
    .sel(Mem__Controle_d[7]), .in_0(banco_de_registradores_16r_1_r_b), .in_1(extensor_16_32_1_s),
    .out(multiplexer_2_out));
  ULA_2_0 ula_2_0_1 (
    .A(banco_de_registradores_16r_1_r_a), .B(multiplexer_2_out), .Func(Mem__Controle_d[6:4]),
    .ZERO(ula_2_0_1_zero), .S(ula_2_0_1_s));
  Multiplexer #(.Bits(24)) multiplexer_3 (
    .sel(ula_2_0_1_zero), .in_0(24'h1), .in_1(ext24bits_2_s), .out(multiplexer_3_out));
  Multiplexer #(.Bits(24)) multiplexer_4 (
    .sel(Mem__Controle_d[0]), .in_0(24'h1), .in_1(multiplexer_3_out), .out(multiplexer_4_out));
  Display display_1 (.A(banco_de_registradores_16r_1_r_a), .E(Mem__Controle_d[2]), .S(Display));

  // Notes on the sheet:
  //   clk: Hz: 2
  //   contents of Mem__Instruções (hex, n*v repeats v):
  //   b001000f,b0020000,b0030001,b0040000,b0050000,c1000000,e1500011
  //   ,b5050001,b4040001,c4000000,e150000e,b5050001,b4040001,e1500007
  //   ,13240000,c4000000,10320000,10430000,b5050001,d000fffa,0,13240000
  //   ,c4000000,f0000000,0,c4000000,f0000000
  //   contents of Mem__Controle (hex, n*v repeats v):
  //   0,8,18,28,38,48,58,68,78,b8,c8,88,4,82,11,6
endmodule
