// Digital circuit R_Shifter_32b.dig as structural Verilog
module R_Shifter_32b (
  input  [31:0] A,
  output [31:0] S
);

  wire r_shifter_16b_1_lsb;

  R_Shifter_16b r_shifter_16b_1 (.Sig(1'b1), .MSB(1'b0), .A(A[31:16]), .S(S[31:16]), .LSB(r_shifter_16b_1_lsb));
  R_Shifter_16b r_shifter_16b_2 (.Sig(1'b1), .MSB(r_shifter_16b_1_lsb), .A(A[15:0]), .S(S[15:0]));  // open: LSB
endmodule
