// Digital circuit R_Shifter_4b.dig as structural Verilog
module R_Shifter_4b (
  input  [3:0] A,
  input  Sig,
  input  MSB,
  output [3:0] S,
  output LSB
);

  Multiplexer multiplexer_1 (.sel(Sig), .in_0(A[3]), .in_1(MSB), .out(S[3]));
  Multiplexer multiplexer_2 (.sel(Sig), .in_0(A[2]), .in_1(A[3]), .out(S[2]));
  Multiplexer multiplexer_3 (.sel(Sig), .in_0(A[1]), .in_1(A[2]), .out(S[1]));
  Multiplexer multiplexer_4 (.sel(Sig), .in_0(A[0]), .in_1(A[1]), .out(S[0]));

  assign LSB = A[0];
endmodule
