// Digital circuit Reg_16b.dig as structural Verilog
module Reg_16b (
  input  CLK,
  input  [15:0] D,
  output [15:0] Q
);

  Reg_4b reg_4b_1 (.D(D[3:0]), .CLK(CLK), .Q(Q[3:0]));
  Reg_4b reg_4b_2 (.D(D[7:4]), .CLK(CLK), .Q(Q[7:4]));
  Reg_4b reg_4b_3 (.D(D[11:8]), .CLK(CLK), .Q(Q[11:8]));
  Reg_4b reg_4b_4 (.D(D[15:12]), .CLK(CLK), .Q(Q[15:12]));
endmodule
