// Digital circuit Reg_32b.dig as structural Verilog
module Reg_32b (
  input  [31:0] D,
  input  CLK,
  output [31:0] Q
);

  Reg_16b reg_16b_1 (.D(D[15:0]), .CLK(CLK), .Q(Q[15:0]));
  Reg_16b reg_16b_2 (.D(D[31:16]), .CLK(CLK), .Q(Q[31:16]));
endmodule
