// Digital circuit Reg_4b.dig as structural Verilog
module Reg_4b (
  input  CLK,
  input  [3:0] D,
  output [3:0] Q
);

  D_FF d_ff_1 (.D(D[0]), .C(CLK), .Q(Q[0]));  // open: nQ
  D_FF d_ff_2 (.D(D[1]), .C(CLK), .Q(Q[1]));  // open: nQ
  D_FF d_ff_3 (.D(D[2]), .C(CLK), .Q(Q[2]));  // open: nQ
  D_FF d_ff_4 (.D(D[3]), .C(CLK), .Q(Q[3]));  // open: nQ
endmodule
