// Digital circuit Somador Look_Ahead.dig as structural Verilog
module Somador_Look_Ahead (
  input  [3:0] A,
  input  [3:0] B,
  input  Cin,
  output C4,
  output [3:0] S
);

  wire _4bit_carry_look_ahead_1_c1, _4bit_carry_look_ahead_1_c2, _4bit_carry_look_ahead_1_c3,
       fulladder_prop_ger_1_gi, fulladder_prop_ger_1_pi, fulladder_prop_ger_2_gi, fulladder_prop_ger_2_pi,
       fulladder_prop_ger_3_gi, fulladder_prop_ger_3_pi, fulladder_prop_ger_4_gi, fulladder_prop_ger_4_pi;

  FullAdder_Prop_Ger fulladder_prop_ger_1 (
    .S(S[3]), .Pi(fulladder_prop_ger_1_pi), .Gi(fulladder_prop_ger_1_gi), .Cin(_4bit_carry_look_ahead_1_c3),
    .A(A[3]), .B(B[3]));
  FullAdder_Prop_Ger fulladder_prop_ger_2 (
    .S(S[2]), .Pi(fulladder_prop_ger_2_pi), .Gi(fulladder_prop_ger_2_gi), .Cin(_4bit_carry_look_ahead_1_c2),
    .A(A[2]), .B(B[2]));
  _4bit_Carry_Look_Ahead _4bit_carry_look_ahead_1 (
    .P3(fulladder_prop_ger_1_pi), .G3(fulladder_prop_ger_1_gi), .C3(_4bit_carry_look_ahead_1_c3),
    .P2(fulladder_prop_ger_2_pi), .G2(fulladder_prop_ger_2_gi), .C2(_4bit_carry_look_ahead_1_c2),
    .P1(fulladder_prop_ger_3_pi), .G1(fulladder_prop_ger_3_gi), .C1(_4bit_carry_look_ahead_1_c1),
    .P0(fulladder_prop_ger_4_pi), .G0(fulladder_prop_ger_4_gi), .Cin(Cin), .C4(C4));
  FullAdder_Prop_Ger fulladder_prop_ger_3 (
    .S(S[1]), .Pi(fulladder_prop_ger_3_pi), .Gi(fulladder_prop_ger_3_gi), .Cin(_4bit_carry_look_ahead_1_c1),
    .A(A[1]), .B(B[1]));
  FullAdder_Prop_Ger fulladder_prop_ger_4 (
    .S(S[0]), .Pi(fulladder_prop_ger_4_pi), .Gi(fulladder_prop_ger_4_gi), .Cin(Cin), .A(A[0]), .B(B[0]));
endmodule
