// Digital circuit Somador_24b.dig as structural Verilog
module Somador_24b (
  input  [23:0] A,
  input  [23:0] B,
  input  Cin,
  output [23:0] S
);

  wire somador_look_ahead_2_c4, somador_look_ahead_16bits_1_cout;

  Somador_Look_Ahead somador_look_ahead_1 (
    .A(A[23:20]), .B(B[23:20]), .S(S[23:20]), .Cin(somador_look_ahead_2_c4));  // open: C4
  Somador_Look_Ahead somador_look_ahead_2 (
    .A(A[19:16]), .B(B[19:16]), .C4(somador_look_ahead_2_c4), .S(S[19:16]),
    .Cin(somador_look_ahead_16bits_1_cout));
  Somador_Look_Ahead_16bits somador_look_ahead_16bits_1 (
    .A(A[15:0]), .B(B[15:0]), .Cout(somador_look_ahead_16bits_1_cout), .S(S[15:0]), .Cin(Cin));
endmodule
