// Digital circuit Somador_Look_Ahead_32_bits.dig as structural Verilog
module Somador_Look_Ahead_32_bits (
  input  [31:0] A,
  input  [31:0] B,
  output [31:0] S
);

  wire somador_look_ahead_16bits_2_cout;

  Somador_Look_Ahead_16bits somador_look_ahead_16bits_1 (
    .A(A[31:16]), .B(B[31:16]), .S(S[31:16]), .Cin(somador_look_ahead_16bits_2_cout));  // open: Cout
  Somador_Look_Ahead_16bits somador_look_ahead_16bits_2 (
    .A(A[15:0]), .B(B[15:0]), .Cout(somador_look_ahead_16bits_2_cout), .S(S[15:0]), .Cin(1'b0));
endmodule
