// Digital circuit ULA 2.0.dig as structural Verilog
module ULA_2_0 (
  input  [31:0] A,
  input  [31:0] B,
  input  [2:0] Func,
  output [31:0] S,
  output ZERO
);

  wire [31:0] a_shift_b_32b_1_s, a_shift_b_r32b_1_s, and_1_s, not_1_s, or_1_s,
       somador_look_ahead_32_bits_1_s, subtrator_look_ahead_32_bits_1_s, xor_1_s;

  Somador_Look_Ahead_32_bits somador_look_ahead_32_bits_1 (.A(A), .B(B), .S(somador_look_ahead_32_bits_1_s));
  Subtrator_Look_Ahead_32_bits subtrator_look_ahead_32_bits_1 (.A(A), .B(B), .S(subtrator_look_ahead_32_bits_1_s));
  AND and_1 (.A(A), .B(B), .S(and_1_s));
  OR or_1 (.A(A), .B(B), .S(or_1_s));
  XOR xor_1 (.A(A), .B(B), .S(xor_1_s));
  NOT not_1 (.A(A), .S(not_1_s));
  A_shift_B_32b a_shift_b_32b_1 (.A(A), .B(B), .S(a_shift_b_32b_1_s));
  A_shift_B_R32b a_shift_b_r32b_1 (.A(A), .B(B), .S(a_shift_b_r32b_1_s));
  Multiplexer #(.Selector_Bits(3), .Bits(32)) multiplexer_1 (
    .sel(Func), .in_0(somador_look_ahead_32_bits_1_s), .in_1(subtrator_look_ahead_32_bits_1_s),
    .in_2(and_1_s), .in_3(or_1_s), .in_4(xor_1_s), .in_5(not_1_s), .in_6(a_shift_b_32b_1_s),
    .in_7(a_shift_b_r32b_1_s), .out(S));
  Zero_32 zero_32_1 (.A(S), .ZERO(ZERO));
endmodule
