// Logisim project sagui.circ as structural Verilog: 8 circuits, main circuit main
module main (
);

  wire BRNC, CLK, EL, ES, JUMP, Mux_Cond, Mux_Inc, Mux_PC, Mux_Ra, Mux_Rb, Reset, WB, WE, ZERO;
  wire [1:0] M_Func, multiplexer_1_out;
  wire [2:0] Func;
  wire [7:0] bancoreg_1_ra_s, Data, Data_Memory_dout, IMM, Instruction_Memory_data, multiplexer_2_out,
       multiplexer_3_out, multiplexer_4_out, multiplexer_5_out, multiplexer_6_out, New_PC, Old_PC, PC_1,
       PC_IMM, RB_S, ula_1_s;

  Clock u_CLK (.out(CLK));
  Button u_Reset (.out(Reset));
  Register PC (.D(New_PC), .en(1'b1), .clk(CLK), .Q(Old_PC), .clr(Reset));
  Somador somador_1 (.A(Old_PC), .B(8'h1), .S(PC_1));
  Somador somador_2 (.A(Old_PC), .B(IMM), .S(PC_IMM));
  ROM Instruction_Memory (.addr(Old_PC), .data(Instruction_Memory_data));
  ROM #(.addrWidth(4), .dataWidth(15)) Control_Memory (
    .addr(Instruction_Memory_data[7:4]),
    .data({Mux_PC, Mux_Inc, Mux_Cond, Mux_Ra, Mux_Rb, WE, Func, M_Func, BRNC, WB, EL, ES}));
  Multiplexer #(.width(2)) multiplexer_1 (
    .in0(2'b00), .in1(Instruction_Memory_data[3:2]), .out(multiplexer_1_out), .sel(Mux_Ra));
  assign IMM = {{4{Instruction_Memory_data[3]}}, Instruction_Memory_data[3:0]};  // Bit_Extender bit_extender_1
  and and_1 (JUMP, ZERO, BRNC);
  Multiplexer #(.width(8)) multiplexer_2 (.in0(PC_1), .in1(PC_IMM), .out(multiplexer_2_out), .sel(JUMP));
  Multiplexer #(.width(8)) multiplexer_3 (.in0(PC_1), .in1(RB_S), .out(multiplexer_3_out), .sel(JUMP));
  BancoReg bancoreg_1 (
    .D(Data), .CLK(CLK), .WE(WE), .RA(multiplexer_1_out), .RB(Instruction_Memory_data[1:0]),
    .RA_S(bancoreg_1_ra_s), .RB_S(RB_S));
  Multiplexer #(.width(8)) multiplexer_4 (.in0(RB_S), .in1(IMM), .out(multiplexer_4_out), .sel(Mux_Rb));
  Multiplexer #(.width(8)) multiplexer_5 (.in0(RB_S), .in1(PC_IMM), .out(multiplexer_5_out), .sel(Mux_Inc));
  Multiplexer #(.width(8)) multiplexer_6 (
    .in0(multiplexer_2_out), .in1(multiplexer_3_out), .out(multiplexer_6_out), .sel(Mux_Cond));
  Multiplexer #(.width(8)) multiplexer_7 (.in0(multiplexer_5_out), .in1(multiplexer_6_out), .out(New_PC), .sel(Mux_PC));
  ULA ula_1 (.A(bancoreg_1_ra_s), .B(multiplexer_4_out), .Func(Func), .MoveFunc(M_Func), .Zero(ZERO), .S(ula_1_s));
  RAM #(.asyncread("true")) Data_Memory (
    .addr(RB_S), .we(ES), .oe(EL), .clk(CLK), .din(ula_1_s), .dout(Data_Memory_dout));
  Multiplexer #(.width(8)) multiplexer_8 (.in0(ula_1_s), .in1(Data_Memory_dout), .out(Data), .sel(WB));

  // Notes on the sheet:
  //   contents of Control_Memory (hex, n*v repeats v):
  //   5948 4148 8 2008 4a06 4941 4b70 4760 4750 4a00 4a40 4a80 4ac0 4b00 4b80 4bc0
endmodule

module Somador (
  input  [7:0] A,
  input  [7:0] B,
  output [7:0] S
);

  Adder adder_1 (.a(A), .b(B), .out(S), .cin(1'b0));  // open: cout
endmodule

module Subtrator (
  input  [7:0] A,
  input  [7:0] B,
  output [7:0] S
);

  wire [7:0] not_1_out;

  Adder adder_1 (.a(A), .b(not_1_out), .out(S), .cin(1'b1));  // open: cout
  assign not_1_out = ~B;  // NOT_Gate not_1, 8 bits wide
endmodule

module ULA (
  input  [7:0] A,
  input  [7:0] B,
  input  [2:0] Func,
  input  [1:0] MoveFunc,
  output Zero,
  output [7:0] S
);

  wire [7:0] and_1_out, moveregimm_1_s, not_1_out, or_1_out, shifter_1_out, shifter_2_out, somador_1_s,
       subtrator_1_s;

  Somador somador_1 (.A(A), .B(B), .S(somador_1_s));
  Subtrator subtrator_1 (.A(A), .B(B), .S(subtrator_1_s));
  assign and_1_out = A & B;  // AND_Gate and_1, 8 bits wide
  assign or_1_out = A | B;  // OR_Gate or_1, 8 bits wide
  assign not_1_out = ~B;  // NOT_Gate not_1, 8 bits wide
  Shifter shifter_1 (.in(A), .\dist (B[2:0]), .out(shifter_1_out));
  Shifter #(.shift("lr")) shifter_2 (.in(A), .\dist (B[2:0]), .out(shifter_2_out));
  MoveRegImm moveregimm_1 (.A(A), .B(B), .MoveFunc(MoveFunc), .S(moveregimm_1_s));
  Multiplexer #(.select(3), .width(8)) multiplexer_1 (
    .in0(somador_1_s), .in1(subtrator_1_s), .in2(and_1_out), .in3(or_1_out), .in4(not_1_out),
    .in5(moveregimm_1_s), .in6(shifter_1_out), .in7(shifter_2_out), .out(S), .sel(Func));
  Zero_Logic zero_logic_1 (.A(S), .Zero(Zero));
endmodule

module Registrador (
  input  [7:0] D,
  input  CLK,
  output [7:0] Q
);

  D_Flip_Flop d_ff_1 (.D(D[0]), .clk(CLK), .Q(Q[0]));  // open: Qn, preset, reset
  D_Flip_Flop d_ff_2 (.D(D[1]), .clk(CLK), .Q(Q[1]));  // open: Qn, preset, reset
  D_Flip_Flop d_ff_3 (.D(D[2]), .clk(CLK), .Q(Q[2]));  // open: Qn, preset, reset
  D_Flip_Flop d_ff_4 (.D(D[3]), .clk(CLK), .Q(Q[3]));  // open: Qn, preset, reset
  D_Flip_Flop d_ff_5 (.D(D[4]), .clk(CLK), .Q(Q[4]));  // open: Qn, preset, reset
  D_Flip_Flop d_ff_6 (.D(D[5]), .clk(CLK), .Q(Q[5]));  // open: Qn, preset, reset
  D_Flip_Flop d_ff_7 (.D(D[6]), .clk(CLK), .Q(Q[6]));  // open: Qn, preset, reset
  D_Flip_Flop d_ff_8 (.D(D[7]), .clk(CLK), .Q(Q[7]));  // open: Qn, preset, reset
endmodule

module BancoReg (
  input  [7:0] D,
  input  CLK,
  input  [1:0] RA,
  input  [1:0] RB,
  input  WE,
  output [7:0] RA_S,
  output [7:0] RB_S
);

  wire W0, W1, W2, W3;
  wire [7:0] multiplexer_1_out, multiplexer_2_out, multiplexer_3_out, multiplexer_4_out, R0, R1, R2, R3;

  Demultiplexer #(.select(2)) demultiplexer_1 (.out0(W0), .out1(W1), .out2(W2), .out3(W3), .in(WE), .sel(RA));
  Multiplexer #(.width(8)) multiplexer_1 (.in0(R0), .in1(D), .out(multiplexer_1_out), .sel(W0));
  Multiplexer #(.width(8)) multiplexer_2 (.in0(R1), .in1(D), .out(multiplexer_2_out), .sel(W1));
  Multiplexer #(.width(8)) multiplexer_3 (.in0(R2), .in1(D), .out(multiplexer_3_out), .sel(W2));
  Multiplexer #(.width(8)) multiplexer_4 (.in0(R3), .in1(D), .out(multiplexer_4_out), .sel(W3));
  Registrador registrador_1 (.D(multiplexer_1_out), .CLK(CLK), .Q(R0));
  Registrador registrador_2 (.D(multiplexer_2_out), .CLK(CLK), .Q(R1));
  Registrador registrador_3 (.D(multiplexer_3_out), .CLK(CLK), .Q(R2));
  Registrador registrador_4 (.D(multiplexer_4_out), .CLK(CLK), .Q(R3));
  Multiplexer #(.select(2), .width(8)) multiplexer_5 (.in0(R0), .in1(R1), .in2(R2), .in3(R3), .out(RA_S), .sel(RA));
  Multiplexer #(.select(2), .width(8)) multiplexer_6 (.in0(R0), .in1(R1), .in2(R2), .in3(R3), .out(RB_S), .sel(RB));
endmodule

module MoveRegImm (
  input  [7:0] A,
  input  [1:0] MoveFunc,
  input  [7:0] B,
  output [7:0] S
);

  Multiplexer #(.select(2), .width(8)) multiplexer_1 (
    .in0(A), .in1({A[7:4], B[3:0]}), .in2({B[3:0], A[3:0]}), .in3(B), .out(S), .sel(MoveFunc));
endmodule

module Zero_Logic (
  input  [7:0] A,
  output Zero
);

  wire [7:0] not_1_out;

  and and_1 (Zero, not_1_out[7], not_1_out[6], not_1_out[5], not_1_out[4], not_1_out[3], not_1_out[2], not_1_out[1], not_1_out[0]);
  assign not_1_out = ~A;  // NOT_Gate not_1, 8 bits wide
endmodule
