// Logisim project SaguiVLIW.circ as structural Verilog: 9 circuits, main circuit Main
module Main (
);

  wire and_1_out, C, pc_logic_1_jump, R, register_21_q, register_22_q, register_23_q, ZERO;
  wire [1:0] forwardingunit_1_mux_brra, forwardingunit_1_mux_brrb, forwardingunit_1_mux_lsmovra,
       forwardingunit_1_mux_lsrb, forwardingunit_1_mux_u1ra, forwardingunit_1_mux_u1rb,
       forwardingunit_1_mux_u2ra, forwardingunit_1_mux_u2rb, register_27_q, register_27_q_2, register_28_q,
       register_28_q_2, register_29_q, register_29_q_2;
  wire [3:0] MemControl_u1control, MemControl_u2control, multiplexer_7_out, multiplexer_8_out,
       multiplexer_9_out, multiplexer_10_out, register_4_q, register_5_q, register_6_q, register_17_q,
       register_18_q, register_19_q, register_20_q;
  wire [4:0] MemControl_bcontrol, multiplexer_6_out, register_3_q;
  wire [5:0] MemControl_lscontrol;
  wire [7:0] adder_1_out, bit_extender_1_out, bit_extender_2_out, InstructionMemory_p2, InstructionMemory_p3,
       InstructionMemory_p4, InstructionMemory_p5, movehighlow_1_move_r, multiplexer_1_out,
       multiplexer_2_out, multiplexer_3_out, multiplexer_4_out, multiplexer_5_out, multiplexer_11_out,
       multiplexer_12_out, multiplexer_13_out, multiplexer_14_out, multiplexer_15_out, multiplexer_16_out,
       multiplexer_17_out, multiplexer_18_out, multiplexer_19_out, multiplexer_20_out, nopreg_1_q,
       nopreg_2_q, nopreg_3_q, nopreg_4_q, pc_logic_1_novo_pc, PC_q, ram_1_dout, register_1_q, register_2_q,
       register_7_q, register_8_q, register_9_q, register_10_q, register_11_q, register_12_q, register_13_q,
       register_14_q, register_15_q, register_16_q, register_24_q, register_25_q, register_26_q,
       RegisterBank_ra1, RegisterBank_ra2, RegisterBank_ra3, RegisterBank_ra4, RegisterBank_rb1,
       RegisterBank_rb2, RegisterBank_rb3, RegisterBank_rb4, ula_1_ula_r, ula_2_ula_r;

  Multiplexer #(.width(8)) multiplexer_1 (
    .in0(adder_1_out), .in1(pc_logic_1_novo_pc), .out(multiplexer_1_out), .sel(pc_logic_1_jump));
  Register PC (.D(multiplexer_1_out), .en(1'b1), .clk(C), .Q(PC_q), .clr(R));
  Adder adder_1 (.a(8'h4), .b(PC_q), .out(adder_1_out), .cin(1'b0));  // open: cout
  // ROM #(.line("quad")) InstructionMemory: pin names not known; wires that end beside it: PC_q, InstructionMemory_p2, InstructionMemory_p3, InstructionMemory_p4, InstructionMemory_p5
  Multiplexer #(.width(8)) multiplexer_2 (
    .in0(InstructionMemory_p2), .in1({8{1'b1}}), .out(multiplexer_2_out));  // open: sel
  Multiplexer #(.width(8)) multiplexer_3 (
    .in0(InstructionMemory_p3), .in1({8{1'b1}}), .out(multiplexer_3_out));  // open: sel
  Multiplexer #(.width(8)) multiplexer_4 (
    .in0(InstructionMemory_p4), .in1({8{1'b1}}), .out(multiplexer_4_out));  // open: sel
  Multiplexer #(.width(8)) multiplexer_5 (
    .in0(InstructionMemory_p5), .in1({8{1'b1}}), .out(multiplexer_5_out));  // open: sel
  Clock CLK (.out(C));
  Button Reset (.out(R));
  Register register_1 (.D(PC_q), .en(1'b1), .Q(register_1_q), .clk(C), .clr(R));
  NopReg nopreg_1 (.D(multiplexer_2_out), .CLK(C), .S(R), .Q(nopreg_1_q));
  NopReg nopreg_2 (.D(multiplexer_3_out), .CLK(C), .S(R), .Q(nopreg_2_q));
  NopReg nopreg_3 (.D(multiplexer_4_out), .CLK(C), .S(R), .Q(nopreg_3_q));
  NopReg nopreg_4 (.D(multiplexer_5_out), .CLK(C), .S(R), .Q(nopreg_4_q));
  assign bit_extender_1_out = {{4{nopreg_1_q[3]}}, nopreg_1_q[3:0]};  // Bit_Extender bit_extender_1
  assign bit_extender_2_out = {{4{nopreg_2_q[3]}}, nopreg_2_q[3:0]};  // Bit_Extender bit_extender_2
  MemoriaControle MemControl (
    .OPCODE2(nopreg_2_q[7:4]), .OPCODE1(nopreg_1_q[7:4]), .OPCODE3(nopreg_3_q[7:4]),
    .OPCODE4(nopreg_4_q[7:4]), .U1Control(MemControl_u1control), .U2Control(MemControl_u2control),
    .LSControl(MemControl_lscontrol), .BControl(MemControl_bcontrol));
  RegistradoresBanco RegisterBank (
    .LSRegs(nopreg_1_q[3:0]), .BRRegs(nopreg_2_q[3:0]), .LSMux(MemControl_lscontrol[0]),
    .BRMux(MemControl_bcontrol[0]), .ULA1Regs(nopreg_3_q[3:0]), .ULA2Regs(nopreg_4_q[3:0]),
    .WEI3(register_22_q), .DataULA1(register_25_q), .WEI4(register_23_q), .DataULA2(register_26_q),
    .WEI1(register_21_q), .DataLWST(register_24_q), .ULA1RaW(register_28_q_2), .ULA2RaW(register_29_q_2),
    .CLK(C), .Reset(R), .LWSTRaW(register_27_q_2), .RB3(RegisterBank_rb3), .RA4(RegisterBank_ra4),
    .RB4(RegisterBank_rb4), .RA1(RegisterBank_ra1), .RB1(RegisterBank_rb1), .RA2(RegisterBank_ra2),
    .RB2(RegisterBank_rb2), .RA3(RegisterBank_ra3));
  PC_Logic pc_logic_1 (
    .PC(register_2_q), .IMM(register_8_q), .RB(multiplexer_12_out), .BRANCH(and_1_out),
    .Mux_Cond(register_4_q[1]), .Mux_In(register_4_q[2]), .Mux_PC(register_4_q[3]),
    .Novo_PC(pc_logic_1_novo_pc), .JUMP(pc_logic_1_jump));
  Multiplexer #(.width(5)) multiplexer_6 (
    .in0(MemControl_lscontrol[5:1]), .in1({5{1'b0}}), .out(multiplexer_6_out));  // open: sel
  Multiplexer #(.width(4)) multiplexer_7 (
    .in0(MemControl_bcontrol[4:1]), .in1(4'b0000), .out(multiplexer_7_out));  // open: sel
  Multiplexer #(.width(4)) multiplexer_8 (
    .in0(MemControl_u1control), .in1(4'b0000), .out(multiplexer_8_out));  // open: sel
  Multiplexer #(.width(4)) multiplexer_9 (
    .in0(MemControl_u2control), .in1(4'b0000), .out(multiplexer_9_out));  // open: sel
  Register register_2 (.D(register_1_q), .en(1'b1), .Q(register_2_q), .clk(C), .clr(R));
  Register #(.width(5)) register_3 (.D(multiplexer_6_out), .en(1'b1), .Q(register_3_q), .clk(C), .clr(R));
  Register #(.width(4)) register_4 (.D(multiplexer_7_out), .en(1'b1), .Q(register_4_q), .clk(C), .clr(R));
  Register #(.width(4)) register_5 (.D(multiplexer_8_out), .en(1'b1), .Q(register_5_q), .clk(C), .clr(R));
  Register #(.width(4)) register_6 (.D(multiplexer_9_out), .en(1'b1), .Q(register_6_q), .clk(C), .clr(R));
  Register register_7 (.D(bit_extender_1_out), .en(1'b1), .Q(register_7_q), .clk(C), .clr(R));
  Register register_8 (.D(bit_extender_2_out), .en(1'b1), .Q(register_8_q), .clk(C), .clr(R));
  Register register_9 (.D(RegisterBank_ra1), .en(1'b1), .Q(register_9_q), .clk(C), .clr(R));
  Register register_10 (.D(RegisterBank_rb1), .en(1'b1), .Q(register_10_q), .clk(C), .clr(R));
  Register register_11 (.D(RegisterBank_ra2), .en(1'b1), .Q(register_11_q), .clk(C), .clr(R));
  Register register_12 (.D(RegisterBank_rb2), .en(1'b1), .Q(register_12_q), .clk(C), .clr(R));
  Register register_13 (.D(RegisterBank_ra3), .en(1'b1), .Q(register_13_q), .clk(C), .clr(R));
  Register register_14 (.D(RegisterBank_rb3), .en(1'b1), .Q(register_14_q), .clk(C), .clr(R));
  Register register_15 (.D(RegisterBank_ra4), .en(1'b1), .Q(register_15_q), .clk(C), .clr(R));
  Register register_16 (.D(RegisterBank_rb4), .en(1'b1), .Q(register_16_q), .clk(C), .clr(R));
  Multiplexer #(.width(4)) multiplexer_10 (
    .in0(4'b0000), .in1(nopreg_1_q[3:0]), .out(multiplexer_10_out));  // open: sel
  Register #(.width(4)) register_17 (.D(multiplexer_10_out), .en(1'b1), .Q(register_17_q), .clk(C), .clr(R));
  Register #(.width(4)) register_18 (.D(nopreg_2_q[3:0]), .en(1'b1), .Q(register_18_q), .clk(C), .clr(R));
  Register #(.width(4)) register_19 (.D(nopreg_3_q[3:0]), .en(1'b1), .Q(register_19_q), .clk(C), .clr(R));
  Register #(.width(4)) register_20 (.D(nopreg_4_q[3:0]), .en(1'b1), .Q(register_20_q), .clk(C), .clr(R));
  Multiplexer #(.select(2), .width(8)) multiplexer_11 (
    .in0(register_11_q), .in1(register_24_q), .in2(register_25_q), .in3(register_26_q),
    .out(multiplexer_11_out), .sel(forwardingunit_1_mux_brra));
  Multiplexer #(.select(2), .width(8)) multiplexer_12 (
    .in0(register_12_q), .in1(register_24_q), .in2(register_25_q), .in3(register_26_q),
    .out(multiplexer_12_out), .sel(forwardingunit_1_mux_brrb));
  Multiplexer #(.select(2), .width(8)) multiplexer_13 (
    .in0(register_9_q), .in1(register_24_q), .in2(register_25_q), .in3(register_26_q),
    .out(multiplexer_13_out), .sel(forwardingunit_1_mux_lsmovra));
  RAM #(.asyncread("true")) ram_1 (
    .addr(multiplexer_14_out), .we(register_3_q[2]), .oe(register_3_q[3]), .clk(C), .din(multiplexer_15_out),
    .dout(ram_1_dout));
  Multiplexer #(.select(2), .width(8)) multiplexer_14 (
    .in0(register_10_q), .in1(register_24_q), .in2(register_25_q), .in3(register_26_q),
    .out(multiplexer_14_out), .sel(forwardingunit_1_mux_lsrb));
  Multiplexer #(.select(2), .width(8)) multiplexer_15 (
    .in0(register_9_q), .in1(register_24_q), .in2(register_25_q), .in3(register_26_q),
    .out(multiplexer_15_out), .sel(forwardingunit_1_mux_lsmovra));
  Multiplexer #(.select(2), .width(8)) multiplexer_16 (
    .in0(register_13_q), .in1(register_24_q), .in2(register_25_q), .in3(register_26_q),
    .out(multiplexer_16_out), .sel(forwardingunit_1_mux_u1ra));
  Multiplexer #(.select(2), .width(8)) multiplexer_17 (
    .in0(register_14_q), .in1(register_24_q), .in2(register_25_q), .in3(register_26_q),
    .out(multiplexer_17_out), .sel(forwardingunit_1_mux_u1rb));
  Multiplexer #(.select(2), .width(8)) multiplexer_18 (
    .in0(register_15_q), .in1(register_24_q), .in2(register_25_q), .in3(register_26_q),
    .out(multiplexer_18_out), .sel(forwardingunit_1_mux_u2ra));
  Multiplexer #(.select(2), .width(8)) multiplexer_19 (
    .in0(register_16_q), .in1(register_24_q), .in2(register_25_q), .in3(register_26_q),
    .out(multiplexer_19_out), .sel(forwardingunit_1_mux_u2rb));
  and and_1 (and_1_out, ZERO, register_4_q[0]);
  Comparator comparator_1 (.a(multiplexer_11_out), .b({8{1'b0}}), .eq(ZERO));  // open: gt, lt
  MoveHighLow movehighlow_1 (
    .A(multiplexer_13_out), .B(register_7_q), .MoveFunc(register_3_q[1]), .Move_R(movehighlow_1_move_r));
  Multiplexer #(.width(8)) multiplexer_20 (
    .in0(movehighlow_1_move_r), .in1(ram_1_dout), .out(multiplexer_20_out), .sel(register_3_q[4]));
  ULA ula_1 (.Ra_S(multiplexer_16_out), .Rb_S(multiplexer_17_out), .Func(register_5_q[3:1]), .ULA_R(ula_1_ula_r));
  ULA ula_2 (.Ra_S(multiplexer_18_out), .Rb_S(multiplexer_19_out), .Func(register_6_q[3:1]), .ULA_R(ula_2_ula_r));
  Register #(.width(1)) register_21 (.D(register_3_q[0]), .en(1'b1), .Q(register_21_q), .clk(C), .clr(R));
  Register #(.width(1)) register_22 (.D(register_5_q[0]), .en(1'b1), .Q(register_22_q), .clk(C), .clr(R));
  Register #(.width(1)) register_23 (.D(register_6_q[0]), .en(1'b1), .Q(register_23_q), .clk(C), .clr(R));
  Register register_24 (.D(multiplexer_20_out), .en(1'b1), .Q(register_24_q), .clk(C), .clr(R));
  Register register_25 (.D(ula_1_ula_r), .en(1'b1), .Q(register_25_q), .clk(C), .clr(R));
  Register register_26 (.D(ula_2_ula_r), .en(1'b1), .Q(register_26_q), .clk(C), .clr(R));
  Register #(.width(4)) register_27 (
    .D(register_17_q), .en(1'b1), .Q({register_27_q_2, register_27_q}), .clk(C), .clr(R));
  Register #(.width(4)) register_28 (
    .D(register_19_q), .en(1'b1), .Q({register_28_q_2, register_28_q}), .clk(C), .clr(R));
  Register #(.width(4)) register_29 (
    .D(register_20_q), .en(1'b1), .Q({register_29_q_2, register_29_q}), .clk(C), .clr(R));
  ForwardingUnit forwardingunit_1 (
    .WE1(register_21_q), .WE3(register_22_q), .WE4(register_23_q),
    .LSRegsAtuais({register_27_q_2, register_27_q}), .U1RegsAtuais({register_28_q_2, register_28_q}),
    .U2RegsAtuais({register_29_q_2, register_29_q}), .LSRegsProx(register_17_q), .BRRegsProx(register_18_q),
    .U1RegsProx(register_19_q), .U2RegsProx(register_20_q), .Mux_U1Ra(forwardingunit_1_mux_u1ra),
    .Mux_U1Rb(forwardingunit_1_mux_u1rb), .Mux_U2Ra(forwardingunit_1_mux_u2ra),
    .Mux_U2Rb(forwardingunit_1_mux_u2rb), .Mux_BRRa(forwardingunit_1_mux_brra),
    .Mux_BRRb(forwardingunit_1_mux_brrb), .Mux_LSMovRa(forwardingunit_1_mux_lsmovra),
    .Mux_LSRb(forwardingunit_1_mux_lsrb));

  // Notes on the sheet:
  //   contents of InstructionMemory (hex, n*v repeats v):
  //   71 ff ff ff 7c ff 84 88 5f ff 8d 91 ff 12 ff ff ff 3e ff ff 7c ff 9a 9f 78 ff 88 8c 7c ff 8c ff 5e
  //   ff 91 8d ff 12 89 ff ff 3e ff ff 78 ff 9a 9f 61 5*ff 88 a3 7c ff ff ff 5e ff 91 89 ff 12 ff ff ff 3e
  //   ff ff 7c ff 9f ff ff ff 8c 98 43 ff 8d ff 52 ff 89 ff 43 ff 8d ff 52 ff 89 ff 43 ff 8d ff 52 ff 89
  //   ff 43 ff 8d ff 52 ff 89 ff 43 ff 8d ff 52 ff 89 ff 43 ff 8d ff 52 ff 89 ff 43 ff 8d ff 52 ff 89 ff
  //   43 ff 8d ff 52 ff 89 ff 43 ff 8d ff 52 ff 89 ff 43 ff 8d ff 52 ff 89 ff 43 ff 8d ff 52 ff 89 ff 43
  //   ff 8d ff 52 ff 89 ff 60 ff ff ff 7c ff 99 9f 4e ff ff 91 40 5*ff 8c ff 5e ff 99 ff ff 12 ff ff ff 3b
  //   ff ff ff 30 14*ff
endmodule

module Shifters (
  input  [7:0] A,
  input  [7:0] B,
  output [7:0] Shift_Left,
  output [7:0] Shift_Right
);

  wire OverFlow;
  wire [7:0] shifter_1_out, shifter_2_out;

  or or_1 (OverFlow, B[3], B[4], B[5], B[6], B[7]);
  Shifter shifter_1 (.in(A), .\dist (B[2:0]), .out(shifter_1_out));
  Shifter #(.shift("lr")) shifter_2 (.in(A), .\dist (B[2:0]), .out(shifter_2_out));
  Multiplexer #(.width(8)) multiplexer_1 (.in0(shifter_1_out), .in1({8{1'b0}}), .out(Shift_Left), .sel(OverFlow));
  Multiplexer #(.width(8)) multiplexer_2 (.in0(shifter_2_out), .in1({8{1'b0}}), .out(Shift_Right), .sel(OverFlow));
endmodule

module ULA (
  input  [7:0] Ra_S,
  input  [7:0] Rb_S,
  input  [2:0] Func,
  output [7:0] ULA_R
);

  wire [7:0] adder_1_out, and_1_out, not_1_out, or_1_out, shifters_1_shift_left, shifters_1_shift_right,
       subtractor_1_out, xor_1_out;

  Adder adder_1 (.a(Ra_S), .b(Rb_S), .out(adder_1_out));  // open: cin, cout
  Subtractor subtractor_1 (.a(Ra_S), .b(Rb_S), .out(subtractor_1_out));  // open: bin, bout
  assign and_1_out = Ra_S & Rb_S;  // AND_Gate and_1, 8 bits wide
  assign or_1_out = Ra_S | Rb_S;  // OR_Gate or_1, 8 bits wide
  assign not_1_out = ~Rb_S;  // NOT_Gate not_1, 8 bits wide
  assign xor_1_out = Ra_S ^ Rb_S;  // XOR_Gate xor_1, 8 bits wide
  Shifters shifters_1 (.A(Ra_S), .B(Rb_S), .Shift_Left(shifters_1_shift_left), .Shift_Right(shifters_1_shift_right));
  Multiplexer #(.select(3), .width(8)) multiplexer_1 (
    .in0(adder_1_out), .in1(subtractor_1_out), .in2(and_1_out), .in3(or_1_out), .in4(not_1_out),
    .in5(xor_1_out), .in6(shifters_1_shift_left), .in7(shifters_1_shift_right), .out(ULA_R), .sel(Func));
endmodule

module MoveHighLow (
  input  [7:0] A,
  input  MoveFunc,
  input  [7:0] B,
  output [7:0] Move_R
);

  Multiplexer #(.width(8)) multiplexer_1 (.in0({A[7:4], B[3:0]}), .in1({B[3:0], A[3:0]}), .out(Move_R), .sel(MoveFunc));
endmodule

module RegistradoresBanco (
  input  CLK,
  input  Reset,
  input  [3:0] LSRegs,
  input  LSMux,
  input  [3:0] BRRegs,
  input  BRMux,
  input  [3:0] ULA1Regs,
  input  [3:0] ULA2Regs,
  input  [1:0] LWSTRaW,
  input  WEI1,
  input  [7:0] DataLWST,
  input  [1:0] ULA1RaW,
  input  WEI3,
  input  [7:0] DataULA1,
  input  [1:0] ULA2RaW,
  input  WEI4,
  input  [7:0] DataULA2,
  output [7:0] RA1,
  output [7:0] RB1,
  output [7:0] RA2,
  output [7:0] RB2,
  output [7:0] RA3,
  output [7:0] RB3,
  output [7:0] RA4,
  output [7:0] RB4
);

  wire and_1_out, and_2_out, and_3_out, and_4_out, and_5_out, and_6_out, and_7_out, and_8_out, and_9_out,
       and_10_out, and_11_out, and_12_out, comparator_1_eq, comparator_2_eq, comparator_3_eq,
       comparator_4_eq, comparator_5_eq, comparator_6_eq, comparator_7_eq, comparator_8_eq, comparator_9_eq,
       comparator_10_eq, comparator_11_eq, comparator_12_eq;
  wire [1:0] BRaR, LRaR, multiplexer_3_out, multiplexer_4_out, multiplexer_5_out, multiplexer_6_out,
       multiplexer_7_out, multiplexer_8_out, multiplexer_9_out, multiplexer_10_out, multiplexer_11_out,
       multiplexer_12_out, multiplexer_13_out, multiplexer_14_out, or_1_out, or_2_out, or_3_out, or_4_out;
  wire [7:0] multiplexer_15_out, multiplexer_16_out, multiplexer_17_out, multiplexer_18_out, R0, R0_q, R1,
       R1_q, R2, R2_q, R3, R3_q;

  Multiplexer #(.width(2)) multiplexer_1 (.in0(2'b00), .in1(LSRegs[3:2]), .out(LRaR), .sel(LSMux));
  Multiplexer #(.width(2)) multiplexer_2 (.in0(2'b00), .in1(BRRegs[3:2]), .out(BRaR), .sel(BRMux));
  Comparator #(.width(2)) comparator_1 (.a(LWSTRaW), .b(2'b00), .eq(comparator_1_eq));  // open: gt, lt
  Comparator #(.width(2)) comparator_2 (.a(ULA1RaW), .b(2'b00), .eq(comparator_2_eq));  // open: gt, lt
  Comparator #(.width(2)) comparator_3 (.a(ULA2RaW), .b(2'b00), .eq(comparator_3_eq));  // open: gt, lt
  Comparator #(.width(2)) comparator_4 (.a(LWSTRaW), .b(2'b01), .eq(comparator_4_eq));  // open: gt, lt
  Comparator #(.width(2)) comparator_5 (.a(ULA1RaW), .b(2'b01), .eq(comparator_5_eq));  // open: gt, lt
  Comparator #(.width(2)) comparator_6 (.a(ULA2RaW), .b(2'b01), .eq(comparator_6_eq));  // open: gt, lt
  Comparator #(.width(2)) comparator_7 (.a(LWSTRaW), .b(2'b10), .eq(comparator_7_eq));  // open: gt, lt
  Comparator #(.width(2)) comparator_8 (.a(ULA1RaW), .b(2'b10), .eq(comparator_8_eq));  // open: gt, lt
  Comparator #(.width(2)) comparator_9 (.a(ULA2RaW), .b(2'b10), .eq(comparator_9_eq));  // open: gt, lt
  Comparator #(.width(2)) comparator_10 (.a(LWSTRaW), .b(2'b11), .eq(comparator_10_eq));  // open: gt, lt
  Comparator #(.width(2)) comparator_11 (.a(ULA1RaW), .b(2'b11), .eq(comparator_11_eq));  // open: gt, lt
  Comparator #(.width(2)) comparator_12 (.a(ULA2RaW), .b(2'b11), .eq(comparator_12_eq));  // open: gt, lt
  and and_1 (and_1_out, comparator_1_eq, WEI1);
  and and_2 (and_2_out, comparator_2_eq, WEI3);
  and and_3 (and_3_out, comparator_3_eq, WEI4);
  and and_4 (and_4_out, comparator_4_eq, WEI1);
  and and_5 (and_5_out, comparator_5_eq, WEI3);
  and and_6 (and_6_out, comparator_6_eq, WEI4);
  and and_7 (and_7_out, comparator_7_eq, WEI1);
  and and_8 (and_8_out, comparator_8_eq, WEI3);
  and and_9 (and_9_out, comparator_9_eq, WEI4);
  and and_10 (and_10_out, comparator_10_eq, WEI1);
  and and_11 (and_11_out, comparator_11_eq, WEI3);
  and and_12 (and_12_out, comparator_12_eq, WEI4);
  Multiplexer #(.width(2)) multiplexer_3 (.in0(2'b00), .in1(2'b01), .out(multiplexer_3_out), .sel(and_1_out));
  Multiplexer #(.width(2)) multiplexer_4 (.in0(2'b00), .in1(2'b10), .out(multiplexer_4_out), .sel(and_2_out));
  Multiplexer #(.width(2)) multiplexer_5 (.in0(2'b00), .in1(2'b11), .out(multiplexer_5_out), .sel(and_3_out));
  Multiplexer #(.width(2)) multiplexer_6 (.in0(2'b00), .in1(2'b01), .out(multiplexer_6_out), .sel(and_4_out));
  Multiplexer #(.width(2)) multiplexer_7 (.in0(2'b00), .in1(2'b10), .out(multiplexer_7_out), .sel(and_5_out));
  Multiplexer #(.width(2)) multiplexer_8 (.in0(2'b00), .in1(2'b11), .out(multiplexer_8_out), .sel(and_6_out));
  Multiplexer #(.width(2)) multiplexer_9 (.in0(2'b00), .in1(2'b01), .out(multiplexer_9_out), .sel(and_7_out));
  Multiplexer #(.width(2)) multiplexer_10 (.in0(2'b00), .in1(2'b10), .out(multiplexer_10_out), .sel(and_8_out));
  Multiplexer #(.width(2)) multiplexer_11 (.in0(2'b00), .in1(2'b11), .out(multiplexer_11_out), .sel(and_9_out));
  Multiplexer #(.width(2)) multiplexer_12 (.in0(2'b00), .in1(2'b01), .out(multiplexer_12_out), .sel(and_10_out));
  Multiplexer #(.width(2)) multiplexer_13 (.in0(2'b00), .in1(2'b10), .out(multiplexer_13_out), .sel(and_11_out));
  Multiplexer #(.width(2)) multiplexer_14 (.in0(2'b00), .in1(2'b11), .out(multiplexer_14_out), .sel(and_12_out));
  assign or_1_out = multiplexer_3_out | multiplexer_4_out | multiplexer_5_out;  // OR_Gate or_1, 2 bits wide
  assign or_2_out = multiplexer_6_out | multiplexer_7_out | multiplexer_8_out;  // OR_Gate or_2, 2 bits wide
  assign or_3_out = multiplexer_9_out | multiplexer_10_out | multiplexer_11_out;  // OR_Gate or_3, 2 bits wide
  assign or_4_out = multiplexer_12_out | multiplexer_13_out | multiplexer_14_out;  // OR_Gate or_4, 2 bits wide
  Multiplexer #(.select(2), .width(8)) multiplexer_15 (
    .in0(R0), .in1(DataLWST), .in2(DataULA1), .in3(DataULA2), .out(multiplexer_15_out), .sel(or_1_out));
  Multiplexer #(.select(2), .width(8)) multiplexer_16 (
    .in0(R1), .in1(DataLWST), .in2(DataULA1), .in3(DataULA2), .out(multiplexer_16_out), .sel(or_2_out));
  Multiplexer #(.select(2), .width(8)) multiplexer_17 (
    .in0(R2), .in1(DataLWST), .in2(DataULA1), .in3(DataULA2), .out(multiplexer_17_out), .sel(or_3_out));
  Multiplexer #(.select(2), .width(8)) multiplexer_18 (
    .in0(R3), .in1(DataLWST), .in2(DataULA1), .in3(DataULA2), .out(multiplexer_18_out), .sel(or_4_out));
  Register #(.trigger("high")) u_R0 (.D(multiplexer_15_out), .en(1'b1), .clk(CLK), .Q(R0_q), .clr(Reset));
  Register #(.trigger("high")) u_R1 (.D(multiplexer_16_out), .en(1'b1), .clk(CLK), .Q(R1_q), .clr(Reset));
  Register #(.trigger("high")) u_R2 (.D(multiplexer_17_out), .en(1'b1), .clk(CLK), .Q(R2_q), .clr(Reset));
  Register #(.trigger("high")) u_R3 (.D(multiplexer_18_out), .en(1'b1), .clk(CLK), .Q(R3_q), .clr(Reset));
  Register #(.trigger("low")) register_1 (.D(R0_q), .en(1'b1), .clk(CLK), .Q(R0), .clr(Reset));
  Register #(.trigger("low")) register_2 (.D(R1_q), .en(1'b1), .clk(CLK), .Q(R1), .clr(Reset));
  Register #(.trigger("low")) register_3 (.D(R2_q), .en(1'b1), .clk(CLK), .Q(R2), .clr(Reset));
  Register #(.trigger("low")) register_4 (.D(R3_q), .en(1'b1), .clk(CLK), .Q(R3), .clr(Reset));
  Multiplexer #(.select(2), .width(8)) multiplexer_19 (.in0(R0), .in1(R1), .in2(R2), .in3(R3), .out(RA1), .sel(LRaR));
  Multiplexer #(.select(2), .width(8)) multiplexer_20 (
    .in0(R0), .in1(R1), .in2(R2), .in3(R3), .out(RB1), .sel(LSRegs[1:0]));
  Multiplexer #(.select(2), .width(8)) multiplexer_21 (.in0(R0), .in1(R1), .in2(R2), .in3(R3), .out(RA2), .sel(BRaR));
  Multiplexer #(.select(2), .width(8)) multiplexer_22 (
    .in0(R0), .in1(R1), .in2(R2), .in3(R3), .out(RB2), .sel(BRRegs[1:0]));
  Multiplexer #(.select(2), .width(8)) multiplexer_23 (
    .in0(R0), .in1(R1), .in2(R2), .in3(R3), .out(RA3), .sel(ULA1Regs[3:2]));
  Multiplexer #(.select(2), .width(8)) multiplexer_24 (
    .in0(R0), .in1(R1), .in2(R2), .in3(R3), .out(RB3), .sel(ULA1Regs[1:0]));
  Multiplexer #(.select(2), .width(8)) multiplexer_25 (
    .in0(R0), .in1(R1), .in2(R2), .in3(R3), .out(RA4), .sel(ULA2Regs[3:2]));
  Multiplexer #(.select(2), .width(8)) multiplexer_26 (
    .in0(R0), .in1(R1), .in2(R2), .in3(R3), .out(RB4), .sel(ULA2Regs[1:0]));

  // Other names for the same wires on the sheet: BRbR[1:0] = BRRegs[1:0]; C = CLK; LData[7:0] = DataLWST;
  //   LRaW[1:0] = LWSTRaW; LRbR[1:0] = LSRegs[1:0]; LWE = WEI1; R = Reset; U1Data[7:0] = DataULA1;
  //   U1RaW[1:0] = ULA1RaW; U1WE = WEI3; U2Data[7:0] = DataULA2; U2RaW[1:0] = ULA2RaW; U2WE = WEI4;
  //   U1RbR[1:0] = ULA1Regs[1:0]; U1RaR[1:0] = ULA1Regs[3:2]; U2RbR[1:0] = ULA2Regs[1:0]; U2RaR[1:0] = ULA2Regs[3:2]

  // Notes on the sheet:
  //   Endereços de Leitura
  //   Endereços de Escrita
endmodule

module MemoriaControle (
  input  [3:0] OPCODE3,
  input  [3:0] OPCODE1,
  input  [3:0] OPCODE4,
  input  [3:0] OPCODE2,
  output [3:0] U1Control,
  output [5:0] LSControl,
  output [3:0] U2Control,
  output [4:0] BControl
);

  wire comparator_1_eq, comparator_2_eq;
  wire [4:0] rom_2_data;
  wire [5:0] rom_1_data;

  ROM #(.addrWidth(2), .dataWidth(6)) rom_1 (.addr(OPCODE1[1:0]), .data(rom_1_data));
  ROM #(.addrWidth(2), .dataWidth(5)) rom_2 (.addr(OPCODE2[1:0]), .data(rom_2_data));
  Comparator #(.mode("unsigned"), .width(4)) comparator_1 (
    .a(OPCODE1), .b(4'b1111), .eq(comparator_1_eq));  // open: gt, lt
  Comparator #(.mode("unsigned"), .width(4)) comparator_2 (
    .a(OPCODE2), .b(4'b1111), .eq(comparator_2_eq));  // open: gt, lt
  Multiplexer #(.width(6)) multiplexer_1 (.in0(rom_1_data), .in1({6{1'b0}}), .out(LSControl), .sel(comparator_1_eq));
  Multiplexer #(.width(5)) multiplexer_2 (.in0(rom_2_data), .in1({5{1'b0}}), .out(BControl), .sel(comparator_2_eq));
  ROM #(.addrWidth(3), .dataWidth(4)) rom_3 (.addr(OPCODE3[2:0]), .data(U1Control));
  ROM #(.addrWidth(3), .dataWidth(4)) rom_4 (.addr(OPCODE4[2:0]), .data(U2Control));

  // Notes on the sheet:
  //   contents of rom_1 (hex, n*v repeats v):
  //   33 9 6 2
  //   contents of rom_2 (hex, n*v repeats v):
  //   7 2 18 10
  //   contents of rom_3 (hex, n*v repeats v):
  //   1 3 5 7 9 d f
  //   contents of rom_4 (hex, n*v repeats v):
  //   1 3 5 7 9 d f
endmodule

module NopReg (
  input  [7:0] D,
  input  S,
  input  CLK,
  output [7:0] Q
);

  D_Flip_Flop d_ff_1 (.D(D[0]), .clk(CLK), .Q(Q[0]), .preset(S));  // open: Qn, reset
  D_Flip_Flop d_ff_2 (.D(D[1]), .clk(CLK), .Q(Q[1]), .preset(S));  // open: Qn, reset
  D_Flip_Flop d_ff_3 (.D(D[2]), .clk(CLK), .Q(Q[2]), .preset(S));  // open: Qn, reset
  D_Flip_Flop d_ff_4 (.D(D[3]), .clk(CLK), .Q(Q[3]), .preset(S));  // open: Qn, reset
  D_Flip_Flop d_ff_5 (.D(D[4]), .clk(CLK), .Q(Q[4]), .preset(S));  // open: Qn, reset
  D_Flip_Flop d_ff_6 (.D(D[5]), .clk(CLK), .Q(Q[5]), .preset(S));  // open: Qn, reset
  D_Flip_Flop d_ff_7 (.D(D[6]), .clk(CLK), .Q(Q[6]), .preset(S));  // open: Qn, reset
  D_Flip_Flop d_ff_8 (.D(D[7]), .clk(CLK), .Q(Q[7]), .preset(S));  // open: Qn, reset
endmodule

module PC_Logic (
  input  [7:0] PC,
  input  [7:0] IMM,
  input  [7:0] RB,
  input  Mux_Cond,
  input  BRANCH,
  input  Mux_PC,
  input  Mux_In,
  output JUMP,
  output [7:0] Novo_PC
);

  wire [7:0] multiplexer_1_out, multiplexer_2_out, PC_IMM, RB_t, shifter_1_out;

  Shifter shifter_1 (.in(IMM), .\dist (3'b010), .out(shifter_1_out));
  Adder adder_1 (.a(PC), .b(shifter_1_out), .out(PC_IMM));  // open: cin, cout
  Shifter shifter_2 (.in(RB), .\dist (3'b010), .out(RB_t));
  Multiplexer #(.width(8)) multiplexer_1 (.in0(PC_IMM), .in1(RB_t), .out(multiplexer_1_out), .sel(Mux_Cond));
  Multiplexer #(.width(8)) multiplexer_2 (.in0(PC_IMM), .in1(RB_t), .out(multiplexer_2_out), .sel(Mux_In));
  Multiplexer #(.width(8)) multiplexer_3 (
    .in0(multiplexer_1_out), .in1(multiplexer_2_out), .out(Novo_PC), .sel(Mux_PC));
  or or_1 (JUMP, BRANCH, Mux_PC);
endmodule

module ForwardingUnit (
  input  WE1,
  input  WE3,
  input  WE4,
  input  [3:0] LSRegsAtuais,
  input  [3:0] U1RegsAtuais,
  input  [3:0] U2RegsAtuais,
  input  [3:0] LSRegsProx,
  input  [3:0] BRRegsProx,
  input  [3:0] U1RegsProx,
  input  [3:0] U2RegsProx,
  output [1:0] Mux_BRRa,
  output [1:0] Mux_BRRb,
  output [1:0] Mux_LSMovRa,
  output [1:0] Mux_LSRb,
  output [1:0] Mux_U1Ra,
  output [1:0] Mux_U1Rb,
  output [1:0] Mux_U2Ra,
  output [1:0] Mux_U2Rb
);

  wire and_1_out, and_2_out, and_3_out, and_4_out, and_5_out, and_6_out, and_7_out, and_8_out, and_9_out,
       and_10_out, and_11_out, and_12_out, and_13_out, and_14_out, and_15_out, and_16_out, and_17_out,
       and_18_out, and_19_out, and_20_out, and_21_out, and_22_out, and_23_out, and_24_out, comparator_1_eq,
       comparator_2_eq, comparator_3_eq, comparator_4_eq, comparator_5_eq, comparator_6_eq, comparator_7_eq,
       comparator_8_eq, comparator_9_eq, comparator_10_eq, comparator_11_eq, comparator_12_eq,
       comparator_13_eq, comparator_14_eq, comparator_15_eq, comparator_16_eq, comparator_17_eq,
       comparator_18_eq, comparator_19_eq, comparator_20_eq, comparator_21_eq, comparator_22_eq,
       comparator_23_eq, comparator_24_eq;
  wire [1:0] multiplexer_1_out, multiplexer_2_out, multiplexer_3_out, multiplexer_4_out, multiplexer_5_out,
       multiplexer_6_out, multiplexer_7_out, multiplexer_8_out, multiplexer_9_out, multiplexer_10_out,
       multiplexer_11_out, multiplexer_12_out, multiplexer_13_out, multiplexer_14_out, multiplexer_15_out,
       multiplexer_16_out, multiplexer_17_out, multiplexer_18_out, multiplexer_19_out, multiplexer_20_out,
       multiplexer_21_out, multiplexer_22_out, multiplexer_23_out, multiplexer_24_out;

  Comparator #(.width(2)) comparator_1 (
    .a(LSRegsAtuais[3:2]), .b(BRRegsProx[3:2]), .eq(comparator_1_eq));  // open: gt, lt
  Comparator #(.width(2)) comparator_2 (
    .a(U1RegsAtuais[3:2]), .b(BRRegsProx[3:2]), .eq(comparator_2_eq));  // open: gt, lt
  Comparator #(.width(2)) comparator_3 (
    .a(U2RegsAtuais[3:2]), .b(BRRegsProx[3:2]), .eq(comparator_3_eq));  // open: gt, lt
  Comparator #(.width(2)) comparator_4 (
    .a(LSRegsAtuais[3:2]), .b(BRRegsProx[1:0]), .eq(comparator_4_eq));  // open: gt, lt
  Comparator #(.width(2)) comparator_5 (
    .a(U1RegsAtuais[3:2]), .b(BRRegsProx[1:0]), .eq(comparator_5_eq));  // open: gt, lt
  Comparator #(.width(2)) comparator_6 (
    .a(U2RegsAtuais[3:2]), .b(BRRegsProx[1:0]), .eq(comparator_6_eq));  // open: gt, lt
  Comparator #(.width(2)) comparator_7 (
    .a(LSRegsAtuais[3:2]), .b(LSRegsProx[3:2]), .eq(comparator_7_eq));  // open: gt, lt
  Comparator #(.width(2)) comparator_8 (
    .a(U1RegsAtuais[3:2]), .b(LSRegsProx[3:2]), .eq(comparator_8_eq));  // open: gt, lt
  Comparator #(.width(2)) comparator_9 (
    .a(U2RegsAtuais[3:2]), .b(LSRegsProx[3:2]), .eq(comparator_9_eq));  // open: gt, lt
  Comparator #(.width(2)) comparator_10 (
    .a(LSRegsAtuais[3:2]), .b(LSRegsProx[1:0]), .eq(comparator_10_eq));  // open: gt, lt
  Comparator #(.width(2)) comparator_11 (
    .a(U1RegsAtuais[3:2]), .b(LSRegsProx[1:0]), .eq(comparator_11_eq));  // open: gt, lt
  Comparator #(.width(2)) comparator_12 (
    .a(U2RegsAtuais[3:2]), .b(LSRegsProx[1:0]), .eq(comparator_12_eq));  // open: gt, lt
  Comparator #(.width(2)) comparator_13 (
    .a(LSRegsAtuais[3:2]), .b(U1RegsProx[3:2]), .eq(comparator_13_eq));  // open: gt, lt
  Comparator #(.width(2)) comparator_14 (
    .a(U1RegsAtuais[3:2]), .b(U1RegsProx[3:2]), .eq(comparator_14_eq));  // open: gt, lt
  Comparator #(.width(2)) comparator_15 (
    .a(U2RegsAtuais[3:2]), .b(U1RegsProx[3:2]), .eq(comparator_15_eq));  // open: gt, lt
  Comparator #(.width(2)) comparator_16 (
    .a(LSRegsAtuais[3:2]), .b(U1RegsProx[1:0]), .eq(comparator_16_eq));  // open: gt, lt
  Comparator #(.width(2)) comparator_17 (
    .a(U1RegsAtuais[3:2]), .b(U1RegsProx[1:0]), .eq(comparator_17_eq));  // open: gt, lt
  Comparator #(.width(2)) comparator_18 (
    .a(U2RegsAtuais[3:2]), .b(U1RegsProx[1:0]), .eq(comparator_18_eq));  // open: gt, lt
  Comparator #(.width(2)) comparator_19 (
    .a(LSRegsAtuais[3:2]), .b(U2RegsProx[3:2]), .eq(comparator_19_eq));  // open: gt, lt
  Comparator #(.width(2)) comparator_20 (
    .a(U1RegsAtuais[3:2]), .b(U2RegsProx[3:2]), .eq(comparator_20_eq));  // open: gt, lt
  Comparator #(.width(2)) comparator_21 (
    .a(U2RegsAtuais[3:2]), .b(U2RegsProx[3:2]), .eq(comparator_21_eq));  // open: gt, lt
  Comparator #(.width(2)) comparator_22 (
    .a(LSRegsAtuais[3:2]), .b(U2RegsProx[1:0]), .eq(comparator_22_eq));  // open: gt, lt
  Comparator #(.width(2)) comparator_23 (
    .a(U1RegsAtuais[3:2]), .b(U2RegsProx[1:0]), .eq(comparator_23_eq));  // open: gt, lt
  Comparator #(.width(2)) comparator_24 (
    .a(U2RegsAtuais[3:2]), .b(U2RegsProx[1:0]), .eq(comparator_24_eq));  // open: gt, lt
  and and_1 (and_1_out, comparator_1_eq, WE1);
  and and_2 (and_2_out, comparator_2_eq, WE3);
  and and_3 (and_3_out, comparator_3_eq, WE4);
  and and_4 (and_4_out, comparator_4_eq, WE1);
  and and_5 (and_5_out, comparator_5_eq, WE3);
  and and_6 (and_6_out, comparator_6_eq, WE4);
  and and_7 (and_7_out, comparator_7_eq, WE1);
  and and_8 (and_8_out, comparator_8_eq, WE3);
  and and_9 (and_9_out, comparator_9_eq, WE4);
  and and_10 (and_10_out, comparator_10_eq, WE1);
  and and_11 (and_11_out, comparator_11_eq, WE3);
  and and_12 (and_12_out, comparator_12_eq, WE4);
  and and_13 (and_13_out, comparator_13_eq, WE1);
  and and_14 (and_14_out, comparator_14_eq, WE3);
  and and_15 (and_15_out, comparator_15_eq, WE4);
  and and_16 (and_16_out, comparator_16_eq, WE1);
  and and_17 (and_17_out, comparator_17_eq, WE3);
  and and_18 (and_18_out, comparator_18_eq, WE4);
  and and_19 (and_19_out, comparator_19_eq, WE1);
  and and_20 (and_20_out, comparator_20_eq, WE3);
  and and_21 (and_21_out, comparator_21_eq, WE4);
  and and_22 (and_22_out, comparator_22_eq, WE1);
  and and_23 (and_23_out, comparator_23_eq, WE3);
  and and_24 (and_24_out, comparator_24_eq, WE4);
  Multiplexer #(.width(2)) multiplexer_1 (.in0(2'b00), .in1(2'b01), .out(multiplexer_1_out), .sel(and_1_out));
  Multiplexer #(.width(2)) multiplexer_2 (.in0(2'b00), .in1(2'b10), .out(multiplexer_2_out), .sel(and_2_out));
  Multiplexer #(.width(2)) multiplexer_3 (.in0(2'b00), .in1(2'b11), .out(multiplexer_3_out), .sel(and_3_out));
  Multiplexer #(.width(2)) multiplexer_4 (.in0(2'b00), .in1(2'b01), .out(multiplexer_4_out), .sel(and_4_out));
  Multiplexer #(.width(2)) multiplexer_5 (.in0(2'b00), .in1(2'b10), .out(multiplexer_5_out), .sel(and_5_out));
  Multiplexer #(.width(2)) multiplexer_6 (.in0(2'b00), .in1(2'b11), .out(multiplexer_6_out), .sel(and_6_out));
  Multiplexer #(.width(2)) multiplexer_7 (.in0(2'b00), .in1(2'b01), .out(multiplexer_7_out), .sel(and_7_out));
  Multiplexer #(.width(2)) multiplexer_8 (.in0(2'b00), .in1(2'b10), .out(multiplexer_8_out), .sel(and_8_out));
  Multiplexer #(.width(2)) multiplexer_9 (.in0(2'b00), .in1(2'b11), .out(multiplexer_9_out), .sel(and_9_out));
  Multiplexer #(.width(2)) multiplexer_10 (.in0(2'b00), .in1(2'b01), .out(multiplexer_10_out), .sel(and_10_out));
  Multiplexer #(.width(2)) multiplexer_11 (.in0(2'b00), .in1(2'b10), .out(multiplexer_11_out), .sel(and_11_out));
  Multiplexer #(.width(2)) multiplexer_12 (.in0(2'b00), .in1(2'b11), .out(multiplexer_12_out), .sel(and_12_out));
  Multiplexer #(.width(2)) multiplexer_13 (.in0(2'b00), .in1(2'b01), .out(multiplexer_13_out), .sel(and_13_out));
  Multiplexer #(.width(2)) multiplexer_14 (.in0(2'b00), .in1(2'b10), .out(multiplexer_14_out), .sel(and_14_out));
  Multiplexer #(.width(2)) multiplexer_15 (.in0(2'b00), .in1(2'b11), .out(multiplexer_15_out), .sel(and_15_out));
  Multiplexer #(.width(2)) multiplexer_16 (.in0(2'b00), .in1(2'b01), .out(multiplexer_16_out), .sel(and_16_out));
  Multiplexer #(.width(2)) multiplexer_17 (.in0(2'b00), .in1(2'b10), .out(multiplexer_17_out), .sel(and_17_out));
  Multiplexer #(.width(2)) multiplexer_18 (.in0(2'b00), .in1(2'b11), .out(multiplexer_18_out), .sel(and_18_out));
  Multiplexer #(.width(2)) multiplexer_19 (.in0(2'b00), .in1(2'b01), .out(multiplexer_19_out), .sel(and_19_out));
  Multiplexer #(.width(2)) multiplexer_20 (.in0(2'b00), .in1(2'b10), .out(multiplexer_20_out), .sel(and_20_out));
  Multiplexer #(.width(2)) multiplexer_21 (.in0(2'b00), .in1(2'b11), .out(multiplexer_21_out), .sel(and_21_out));
  Multiplexer #(.width(2)) multiplexer_22 (.in0(2'b00), .in1(2'b01), .out(multiplexer_22_out), .sel(and_22_out));
  Multiplexer #(.width(2)) multiplexer_23 (.in0(2'b00), .in1(2'b10), .out(multiplexer_23_out), .sel(and_23_out));
  Multiplexer #(.width(2)) multiplexer_24 (.in0(2'b00), .in1(2'b11), .out(multiplexer_24_out), .sel(and_24_out));
  assign Mux_BRRa = multiplexer_1_out | multiplexer_2_out | multiplexer_3_out;  // OR_Gate or_1, 2 bits wide
  assign Mux_BRRb = multiplexer_4_out | multiplexer_5_out | multiplexer_6_out;  // OR_Gate or_2, 2 bits wide
  assign Mux_LSMovRa = multiplexer_7_out | multiplexer_8_out | multiplexer_9_out;  // OR_Gate or_3, 2 bits wide
  assign Mux_LSRb = multiplexer_10_out | multiplexer_11_out | multiplexer_12_out;  // OR_Gate or_4, 2 bits wide
  assign Mux_U1Ra = multiplexer_13_out | multiplexer_14_out | multiplexer_15_out;  // OR_Gate or_5, 2 bits wide
  assign Mux_U1Rb = multiplexer_16_out | multiplexer_17_out | multiplexer_18_out;  // OR_Gate or_6, 2 bits wide
  assign Mux_U2Ra = multiplexer_19_out | multiplexer_20_out | multiplexer_21_out;  // OR_Gate or_7, 2 bits wide
  assign Mux_U2Rb = multiplexer_22_out | multiplexer_23_out | multiplexer_24_out;  // OR_Gate or_8, 2 bits wide

  // Other names for the same wires on the sheet: BRRbP[1:0] = BRRegsProx[1:0]; BRRaP[1:0] = BRRegsProx[3:2];
  //   LSRaA[1:0] = LSRegsAtuais[3:2]; LSRbP[1:0] = LSRegsProx[1:0]; LSRaP[1:0] = LSRegsProx[3:2];
  //   U1RaA[1:0] = U1RegsAtuais[3:2]; U1RbP[1:0] = U1RegsProx[1:0]; U1RaP[1:0] = U1RegsProx[3:2];
  //   U2RaA[1:0] = U2RegsAtuais[3:2]; U2RbP[1:0] = U2RegsProx[1:0]; U2RaP[1:0] = U2RegsProx[3:2]
endmodule
