// Digital circuit P_botao.dig as structural Verilog
module P_botao (
  input  CLK,
  input  B,
  output VmP,
  output VeP
);

  wire and_1_out, and_2_out, and_3_out, and_4_out, and_5_out, and_6_out, not_1_out, not_2_out, not_3_out,
       not_4_out, or_1_out, or_2_out, W0_q, W1_q;

  not not_1 (not_1_out, B);
  not not_2 (not_2_out, VeP);
  not not_3 (not_3_out, W1_q);
  not not_4 (not_4_out, W0_q);
  and and_1 (and_1_out, VeP, not_3_out, not_4_out);
  and and_2 (and_2_out, not_1_out, not_2_out, not_3_out, W0_q);
  and and_3 (and_3_out, not_2_out, W1_q, not_4_out);
  and and_4 (and_4_out, not_2_out, not_4_out);
  and and_5 (and_5_out, B, not_2_out, W1_q);
  and and_6 (and_6_out, B, not_2_out, W0_q);
  or or_1 (or_1_out, and_1_out, and_2_out, and_3_out);
  or or_2 (or_2_out, and_4_out, and_5_out);
  D_FF W2 (.D(and_6_out), .C(CLK), .Q(VeP));  // open: nQ
  D_FF W1 (.D(or_1_out), .C(CLK), .Q(W1_q));  // open: nQ
  D_FF W0 (.D(or_2_out), .C(CLK), .Q(W0_q));  // open: nQ
  not not_5 (VmP, VeP);
endmodule
