// Digital circuit S1_S3_botao.dig as structural Verilog
module S1_S3_botao (
  input  CLK,
  input  B,
  output S2,
  output S1,
  output S0
);

  wire and_1_out, and_2_out, and_3_out, and_4_out, and_5_out, and_6_out, not_1_out, not_2_out, not_3_out,
       not_4_out, not_5_out, not_6_out, not_7_out, not_8_out, not_9_out, or_1_out, or_2_out, W0_q, W1_q, W2_q;

  not not_1 (not_1_out, B);
  not not_2 (not_2_out, W2_q);
  not not_3 (not_3_out, W1_q);
  not not_4 (not_4_out, W0_q);
  and and_1 (and_1_out, W2_q, not_3_out, not_4_out);
  and and_2 (and_2_out, not_1_out, not_2_out, not_3_out, W0_q);
  and and_3 (and_3_out, not_2_out, W1_q, not_4_out);
  and and_4 (and_4_out, not_2_out, not_4_out);
  and and_5 (and_5_out, B, not_2_out, W1_q);
  and and_6 (and_6_out, B, not_2_out, W0_q);
  or or_1 (or_1_out, and_1_out, and_2_out, and_3_out);
  or or_2 (or_2_out, and_4_out, and_5_out);
  D_FF W2 (.D(and_6_out), .C(CLK), .Q(W2_q));  // open: nQ
  D_FF W1 (.D(or_1_out), .C(CLK), .Q(W1_q));  // open: nQ
  D_FF W0 (.D(or_2_out), .C(CLK), .Q(W0_q));  // open: nQ
  or or_3 (S2, W2_q, W1_q);
  and and_7 (S1, not_5_out, not_6_out, W0_q);
  not not_5 (not_5_out, W2_q);
  not not_6 (not_6_out, W1_q);
  and and_8 (S0, not_7_out, not_8_out, not_9_out);
  not not_7 (not_7_out, W2_q);
  not not_8 (not_8_out, W1_q);
  not not_9 (not_9_out, W0_q);
endmodule
