// Digital circuit S2_botao.dig as structural Verilog
module S2_botao (
  input  CLK,
  input  B,
  output VmS3,
  output AmS3,
  output VeS3
);

  wire and_1_out, and_2_out, and_3_out, and_4_out, and_5_out, and_6_out, not_1_out, not_2_out, not_3_out,
       not_4_out, not_5_out, or_1_out, or_2_out, W3_q, W4_q, W5_q;

  not not_1 (not_1_out, B);
  not not_2 (not_2_out, W5_q);
  not not_3 (not_3_out, W4_q);
  not not_4 (not_4_out, W3_q);
  and and_1 (and_1_out, W5_q, not_3_out, not_4_out);
  and and_2 (and_2_out, not_1_out, not_2_out, not_3_out, W3_q);
  and and_3 (and_3_out, not_2_out, W4_q, not_4_out);
  and and_4 (and_4_out, not_2_out, not_4_out);
  and and_5 (and_5_out, B, not_2_out, W4_q);
  and and_6 (and_6_out, B, not_2_out, W3_q);
  or or_1 (or_1_out, and_1_out, and_2_out, and_3_out);
  or or_2 (or_2_out, and_4_out, and_5_out);
  D_FF W5 (.D(and_6_out), .C(CLK), .Q(W5_q));  // open: nQ
  D_FF W4 (.D(or_1_out), .C(CLK), .Q(W4_q));  // open: nQ
  D_FF W3 (.D(or_2_out), .C(CLK), .Q(W3_q));  // open: nQ
  not not_5 (not_5_out, W3_q);
  and and_7 (AmS3, W4_q, W3_q);
  and and_8 (VeS3, W4_q, not_5_out);
  not not_6 (VmS3, W4_q);
endmodule
