// Digital circuit Trabalho_Semáforos.dig as structural Verilog
module \Trabalho_Semáforos  (
  input  Clock
);

  wire B_out, p_botao_1_vep, p_botao_1_vmp, p_botao_2_vep, p_botao_2_vmp, rs_ff_as_1_q, s1_s3_botao_1_s0,
       s1_s3_botao_1_s1, s1_s3_botao_1_s2, s1_s3_botao_2_s0, s1_s3_botao_2_s1, s1_s3_botao_2_s2,
       s2_botao_1_ams3, s2_botao_1_ves3, s2_botao_1_vms3;

  Button B (.out(B_out));
  RS_FF_AS rs_ff_as_1 (.S(B_out), .R(p_botao_2_vep), .Q(rs_ff_as_1_q));  // open: nQ
  S1_S3_botao s1_s3_botao_1 (
    .CLK(Clock), .B(rs_ff_as_1_q), .S2(s1_s3_botao_1_s2), .S1(s1_s3_botao_1_s1), .S0(s1_s3_botao_1_s0));
  S2_botao s2_botao_1 (
    .CLK(Clock), .B(rs_ff_as_1_q), .VmS3(s2_botao_1_vms3), .AmS3(s2_botao_1_ams3), .VeS3(s2_botao_1_ves3));
  S1_S3_botao s1_s3_botao_2 (
    .CLK(Clock), .B(rs_ff_as_1_q), .S2(s1_s3_botao_2_s2), .S1(s1_s3_botao_2_s1), .S0(s1_s3_botao_2_s0));
  LED led_1 (.in(s1_s3_botao_1_s2));
  LED led_2 (.in(s1_s3_botao_1_s1));
  LED led_3 (.in(s1_s3_botao_1_s0));
  LED led_4 (.in(s2_botao_1_vms3));
  LED led_5 (.in(s2_botao_1_ams3));
  LED led_6 (.in(s2_botao_1_ves3));
  LED led_7 (.in(s1_s3_botao_2_s2));
  LED led_8 (.in(s1_s3_botao_2_s1));
  LED led_9 (.in(s1_s3_botao_2_s0));
  P_botao p_botao_1 (.CLK(Clock), .B(rs_ff_as_1_q), .VmP(p_botao_1_vmp), .VeP(p_botao_1_vep));
  P_botao p_botao_2 (.CLK(Clock), .B(rs_ff_as_1_q), .VmP(p_botao_2_vmp), .VeP(p_botao_2_vep));
  LED led_10 (.in(p_botao_1_vmp));
  LED led_11 (.in(p_botao_1_vep));
  LED led_12 (.in(p_botao_2_vmp));
  LED led_13 (.in(p_botao_2_vep));
endmodule
