// Digital circuit 16P1.dig as structural Verilog
module _16P1 (
  input  [15:0] E1,
  output S0
);

  wire or_1_out, or_2_out, or_3_out, or_4_out, or_5_out, or_6_out;

  or or_1 (or_1_out, E1[0], E1[1], E1[2], E1[3], E1[4]);
  or or_2 (or_2_out, or_1_out, or_4_out);
  or or_3 (or_3_out, or_2_out, or_6_out);
  or or_4 (or_4_out, E1[5], E1[6], E1[7], E1[8], E1[9]);
  not not_1 (S0, or_3_out);
  or or_5 (or_5_out, E1[10], E1[11], E1[12], E1[13], E1[14]);
  or or_6 (or_6_out, or_5_out, E1[15]);
endmodule
