// Digital circuit Comparador16bits.dig as structural Verilog
module Comparador16bits (
  input  [15:0] A,
  input  [15:0] B,
  output Y__A__eq__B,
  output X__A__lt__B,
  output Z__A__gt__B
);

  wire and_1_out, and_2_out, comparador8bits_1_x__a__lt__b, comparador8bits_1_y__a__eq__b,
       comparador8bits_1_z__a__gt__b, comparador8bits_2_x__a__lt__b, comparador8bits_2_y__a__eq__b,
       comparador8bits_2_z__a__gt__b, xnor_1_out;

  Comparador8bits comparador8bits_1 (
    .A(A[15:8]), .B(B[15:8]), .X__A__lt__B(comparador8bits_1_x__a__lt__b),
    .Y__A__eq__B(comparador8bits_1_y__a__eq__b), .Z__A__gt__B(comparador8bits_1_z__a__gt__b));
  Comparador8bits comparador8bits_2 (
    .A(A[7:0]), .B(B[7:0]), .X__A__lt__B(comparador8bits_2_x__a__lt__b),
    .Y__A__eq__B(comparador8bits_2_y__a__eq__b), .Z__A__gt__B(comparador8bits_2_z__a__gt__b));
  and and_1 (and_1_out, comparador8bits_1_y__a__eq__b, comparador8bits_2_x__a__lt__b);
  and and_2 (and_2_out, comparador8bits_1_y__a__eq__b, comparador8bits_2_z__a__gt__b);
  xnor xnor_1 (xnor_1_out, comparador8bits_2_y__a__eq__b, comparador8bits_1_y__a__eq__b);
  or or_1 (X__A__lt__B, comparador8bits_1_x__a__lt__b, and_1_out);
  and and_3 (Y__A__eq__B, comparador8bits_1_y__a__eq__b, xnor_1_out);
  or or_2 (Z__A__gt__B, and_2_out, comparador8bits_1_z__a__gt__b);
endmodule
