// Digital circuit Comparador16x16bits.dig as structural Verilog
module Comparador16x16bits (
  input  [15:0] A,
  input  [15:0] B,
  output [15:0] A__eq__B,
  output [15:0] A__gt__B,
  output [15:0] A__lt__B
);

  wire comparador16bits_1_x__a__lt__b, comparador16bits_1_y__a__eq__b, comparador16bits_1_z__a__gt__b;

  Comparador16bits comparador16bits_1 (
    .A(A), .B(B), .X__A__lt__B(comparador16bits_1_x__a__lt__b), .Y__A__eq__B(comparador16bits_1_y__a__eq__b),
    .Z__A__gt__B(comparador16bits_1_z__a__gt__b));
  _1P16 _1p16_1 (.A(comparador16bits_1_x__a__lt__b), .S(A__lt__B));
  _1P16 _1p16_2 (.A(comparador16bits_1_y__a__eq__b), .S(A__eq__B));
  _1P16 _1p16_3 (.A(comparador16bits_1_z__a__gt__b), .S(A__gt__B));
endmodule
