// Digital circuit Comparador1bit.dig as structural Verilog
module Comparador1bit (
  input  A,
  input  B,
  output X__A__lt__B,
  output Z__A__gt__B,
  output Y__A__eq__B
);

  wire not_1_out, not_2_out;

  not not_1 (not_1_out, A);
  not not_2 (not_2_out, B);
  and and_1 (X__A__lt__B, not_1_out, B);
  xnor xnor_1 (Y__A__eq__B, A, B);
  and and_2 (Z__A__gt__B, A, not_2_out);
endmodule
