// Digital circuit Comparador2bits.dig as structural Verilog
module Comparador2bits (
  input  [1:0] A,
  input  [1:0] B,
  output X__A__lt__B,
  output Z__A__gt__B,
  output Y__A__eq__B
);

  wire and_1_out, and_2_out, comparador1bit_1_x__a__lt__b, comparador1bit_1_y__a__eq__b,
       comparador1bit_1_z__a__gt__b, not_1_out, not_2_out, xnor_1_out;

  Comparador1bit comparador1bit_1 (
    .A(A[1]), .B(B[1]), .X__A__lt__B(comparador1bit_1_x__a__lt__b),
    .Y__A__eq__B(comparador1bit_1_y__a__eq__b), .Z__A__gt__B(comparador1bit_1_z__a__gt__b));
  not not_1 (not_1_out, A[0]);
  not not_2 (not_2_out, B[0]);
  and and_1 (and_1_out, comparador1bit_1_y__a__eq__b, not_1_out, B[0]);
  xnor xnor_1 (xnor_1_out, A[0], B[0]);
  and and_2 (and_2_out, comparador1bit_1_y__a__eq__b, A[0], not_2_out);
  or or_1 (X__A__lt__B, comparador1bit_1_x__a__lt__b, and_1_out);
  and and_3 (Y__A__eq__B, comparador1bit_1_y__a__eq__b, xnor_1_out);
  or or_2 (Z__A__gt__B, and_2_out, comparador1bit_1_z__a__gt__b);
endmodule
