// Digital circuit Comparador4bits.dig as structural Verilog
module Comparador4bits (
  input  [3:0] A,
  input  [3:0] B,
  output X__A__lt__B,
  output Z__A__gt__B,
  output Y__A__eq__B
);

  wire and_1_out, and_2_out, comparador3bits_1_x__a__lt__b, comparador3bits_1_y__a__eq__b,
       comparador3bits_1_z__a__gt__b, not_1_out, not_2_out, xnor_1_out;

  Comparador3bits comparador3bits_1 (
    .A(A[3:1]), .B(B[3:1]), .X__A__lt__B(comparador3bits_1_x__a__lt__b),
    .Y__A__eq__B(comparador3bits_1_y__a__eq__b), .Z__A__gt__B(comparador3bits_1_z__a__gt__b));
  not not_1 (not_1_out, A[0]);
  not not_2 (not_2_out, B[0]);
  and and_1 (and_1_out, not_1_out, B[0], comparador3bits_1_y__a__eq__b);
  and and_2 (and_2_out, A[0], not_2_out, comparador3bits_1_y__a__eq__b);
  xnor xnor_1 (xnor_1_out, A[0], B[0]);
  or or_1 (X__A__lt__B, comparador3bits_1_x__a__lt__b, and_1_out);
  and and_3 (Y__A__eq__B, comparador3bits_1_y__a__eq__b, xnor_1_out);
  or or_2 (Z__A__gt__B, and_2_out, comparador3bits_1_z__a__gt__b);
endmodule
