// Digital circuit Comparador8bits.dig as structural Verilog
module Comparador8bits (
  input  [7:0] A,
  input  [7:0] B,
  output X__A__lt__B,
  output Z__A__gt__B,
  output Y__A__eq__B
);

  wire and_1_out, and_2_out, comparador4bits_1_x__a__lt__b, comparador4bits_1_y__a__eq__b,
       comparador4bits_1_z__a__gt__b, comparador4bits_2_x__a__lt__b, comparador4bits_2_y__a__eq__b,
       comparador4bits_2_z__a__gt__b;

  Comparador4bits comparador4bits_1 (
    .X__A__lt__B(comparador4bits_1_x__a__lt__b), .Y__A__eq__B(comparador4bits_1_y__a__eq__b),
    .Z__A__gt__B(comparador4bits_1_z__a__gt__b), .A(A[7:4]), .B(B[7:4]));
  Comparador4bits comparador4bits_2 (
    .X__A__lt__B(comparador4bits_2_x__a__lt__b), .Y__A__eq__B(comparador4bits_2_y__a__eq__b),
    .Z__A__gt__B(comparador4bits_2_z__a__gt__b), .A(A[3:0]), .B(B[3:0]));
  and and_1 (and_1_out, comparador4bits_1_y__a__eq__b, comparador4bits_2_x__a__lt__b);
  and and_2 (and_2_out, comparador4bits_1_y__a__eq__b, comparador4bits_2_z__a__gt__b);
  or or_1 (X__A__lt__B, comparador4bits_1_x__a__lt__b, and_1_out);
  and and_3 (Y__A__eq__B, comparador4bits_1_y__a__eq__b, comparador4bits_2_y__a__eq__b);
  or or_2 (Z__A__gt__B, comparador4bits_1_z__a__gt__b, and_2_out);
endmodule
