// Digital circuit FullAdder.dig as structural Verilog
module FullAdder (
  input  B,
  input  A,
  input  Cin,
  output S,
  output Cout
);

  wire and_1_out, and_2_out, or_2_out;

  or or_1 (Cout, and_1_out, and_2_out);
  and and_1 (and_1_out, or_2_out, Cin);
  and and_2 (and_2_out, A, B);
  or or_2 (or_2_out, A, B);
  xor xor_1 (S, Cin, B, A);
endmodule
