// Digital circuit FullAdder16bits.dig as structural Verilog
module FullAdder16bits (
  input  [15:0] A,
  input  [15:0] B,
  output [15:0] S
);

  wire fulladder4bitsv2_1_cout, fulladder4bitsv2_2_cout, fulladder4bitsv2_3_cout;

  FullAdder4BitsV2 fulladder4bitsv2_1 (.A(A[3:0]), .B(B[3:0]), .Cin(1'b0), .S(S[3:0]), .Cout(fulladder4bitsv2_1_cout));
  FullAdder4BitsV2 fulladder4bitsv2_2 (
    .A(A[7:4]), .B(B[7:4]), .Cin(fulladder4bitsv2_1_cout), .S(S[7:4]), .Cout(fulladder4bitsv2_2_cout));
  FullAdder4BitsV2 fulladder4bitsv2_3 (
    .A(A[11:8]), .B(B[11:8]), .Cin(fulladder4bitsv2_2_cout), .S(S[11:8]), .Cout(fulladder4bitsv2_3_cout));
  FullAdder4BitsV2 fulladder4bitsv2_4 (
    .A(A[15:12]), .B(B[15:12]), .Cin(fulladder4bitsv2_3_cout), .S(S[15:12]));  // open: Cout
endmodule
