// Digital circuit FullAdder2bits.dig as structural Verilog
module FullAdder2bits (
  input  Cin,
  input  A0,
  input  B0,
  input  A1,
  input  B1,
  output S0,
  output S1,
  output Cout
);

  wire fulladder_2_cout;

  FullAdder fulladder_1 (.B(B1), .A(A1), .Cin(fulladder_2_cout), .S(S1), .Cout(Cout));
  FullAdder fulladder_2 (.B(B0), .A(A0), .Cin(Cin), .S(S0), .Cout(fulladder_2_cout));
endmodule
