// Digital circuit FullAdder4BitsV2.dig as structural Verilog
module FullAdder4BitsV2 (
  input  [3:0] A,
  input  [3:0] B,
  input  Cin,
  output [3:0] S,
  output Cout
);

  wire fulladder2bits_1_cout;

  FullAdder2bits fulladder2bits_1 (
    .Cin(Cin), .A0(A[0]), .B0(B[0]), .A1(A[1]), .B1(B[1]), .S0(S[0]), .S1(S[1]), .Cout(fulladder2bits_1_cout));
  FullAdder2bits fulladder2bits_2 (
    .Cin(fulladder2bits_1_cout), .A0(A[2]), .B0(B[2]), .A1(A[3]), .B1(B[3]), .S0(S[2]), .S1(S[3]), .Cout(Cout));
endmodule
