// Digital circuit Subtrator16bits.dig as structural Verilog
module Subtrator16bits (
  input  [15:0] A,
  input  [15:0] B,
  output [15:0] S,
  output Cout
);

  wire [15:0] not_1_out;

  assign not_1_out = ~B;  // Not not_1, 16 bits wide
  FA16CIN1 fa16cin1_1 (.A(A), .B(not_1_out), .S(S), .Cout(Cout));
endmodule
