// Digital circuit ULA100%.dig as structural Verilog
module ULA100 (
  input  [15:0] A,
  input  [15:0] B,
  input  [2:0] FUNC,
  output [15:0] R,
  output ZERO
);

  wire [15:0] and_1_out, comparador16x16bits_1_a__eq__b, comparador16x16bits_1_a__gt__b,
       comparador16x16bits_1_a__lt__b, fulladder16bits_1_s, not_1_out, or_1_out, subtrator16bits_1_s;

  FullAdder16bits fulladder16bits_1 (.A(A), .B(B), .S(fulladder16bits_1_s));
  Subtrator16bits subtrator16bits_1 (.A(A), .B(B), .S(subtrator16bits_1_s));  // open: Cout
  assign and_1_out = B & A;  // And and_1, 16 bits wide
  assign or_1_out = B | A;  // Or or_1, 16 bits wide
  assign not_1_out = ~A;  // Not not_1, 16 bits wide
  Comparador16x16bits comparador16x16bits_1 (
    .A(A), .B(B), .A__eq__B(comparador16x16bits_1_a__eq__b), .A__gt__B(comparador16x16bits_1_a__gt__b),
    .A__lt__B(comparador16x16bits_1_a__lt__b));
  Multiplexer #(.Selector_Bits(3), .Bits(16)) multiplexer_1 (
    .sel(FUNC), .in_0(fulladder16bits_1_s), .in_1(subtrator16bits_1_s), .in_2(and_1_out), .in_3(or_1_out),
    .in_4(not_1_out), .in_5(comparador16x16bits_1_a__eq__b), .in_6(comparador16x16bits_1_a__gt__b),
    .in_7(comparador16x16bits_1_a__lt__b), .out(R));
  _16P1 _16p1_1 (.E1(R), .S0(ZERO));
endmodule
