// Digital circuit 4bit_Carry_Look_Ahead.dig as structural Verilog
module _4bit_Carry_Look_Ahead (
  input  P0,
  input  G0,
  input  Cin,
  input  G1,
  input  P1,
  input  G2,
  input  P2,
  input  P3,
  input  G3,
  output C1,
  output C4,
  output C2,
  output C3
);

  wire and_1_out, and_2_out, and_3_out, and_4_out;

  or or_1 (C4, G3, and_1_out);
  and and_1 (and_1_out, C3, P3);
  or or_2 (C3, and_2_out, G2);
  and and_2 (and_2_out, C2, P2);
  or or_3 (C2, and_3_out, G1);
  and and_3 (and_3_out, C1, P1);
  or or_4 (C1, and_4_out, G0);
  and and_4 (and_4_out, Cin, P0);
endmodule
