// Digital circuit A_shift_B_32b.dig as structural Verilog
module A_shift_B_32b (
  input  [31:0] A,
  input  [31:0] B,
  output [31:0] S
);

  wire [31:0] shifter_2__32b_1_s, shifter_2__32b_2_s, shifter_2__32b_3_s, shifter_2__32b_4_s,
       shifter_2__32b_5_s, shifter_2__32b_6_s, shifter_2__32b_7_s, shifter_2__32b_8_s, shifter_2__32b_9_s,
       shifter_2__32b_10_s, shifter_2__32b_11_s, shifter_2__32b_12_s, shifter_2__32b_13_s,
       shifter_2__32b_14_s, shifter_2__32b_15_s, shifter_2__32b_16_s, shifter_2__32b_17_s,
       shifter_2__32b_18_s, shifter_2__32b_19_s, shifter_2__32b_20_s, shifter_2__32b_21_s,
       shifter_2__32b_22_s, shifter_2__32b_23_s, shifter_2__32b_24_s, shifter_2__32b_25_s,
       shifter_2__32b_26_s, shifter_2__32b_27_s, shifter_2__32b_28_s, shifter_2__32b_29_s,
       shifter_2__32b_30_s, shifter_2__32b_31_s;

  shifter_2__32b shifter_2__32b_1 (.A(A), .S(shifter_2__32b_1_s));
  shifter_2__32b shifter_2__32b_2 (.A(shifter_2__32b_1_s), .S(shifter_2__32b_2_s));
  shifter_2__32b shifter_2__32b_3 (.A(shifter_2__32b_2_s), .S(shifter_2__32b_3_s));
  shifter_2__32b shifter_2__32b_4 (.A(shifter_2__32b_3_s), .S(shifter_2__32b_4_s));
  shifter_2__32b shifter_2__32b_5 (.A(shifter_2__32b_4_s), .S(shifter_2__32b_5_s));
  shifter_2__32b shifter_2__32b_6 (.A(shifter_2__32b_5_s), .S(shifter_2__32b_6_s));
  shifter_2__32b shifter_2__32b_7 (.A(shifter_2__32b_6_s), .S(shifter_2__32b_7_s));
  shifter_2__32b shifter_2__32b_8 (.A(shifter_2__32b_7_s), .S(shifter_2__32b_8_s));
  shifter_2__32b shifter_2__32b_9 (.A(shifter_2__32b_8_s), .S(shifter_2__32b_9_s));
  shifter_2__32b shifter_2__32b_10 (.A(shifter_2__32b_9_s), .S(shifter_2__32b_10_s));
  shifter_2__32b shifter_2__32b_11 (.A(shifter_2__32b_10_s), .S(shifter_2__32b_11_s));
  shifter_2__32b shifter_2__32b_12 (.A(shifter_2__32b_11_s), .S(shifter_2__32b_12_s));
  shifter_2__32b shifter_2__32b_13 (.A(shifter_2__32b_12_s), .S(shifter_2__32b_13_s));
  shifter_2__32b shifter_2__32b_14 (.A(shifter_2__32b_13_s), .S(shifter_2__32b_14_s));
  shifter_2__32b shifter_2__32b_15 (.A(shifter_2__32b_14_s), .S(shifter_2__32b_15_s));
  shifter_2__32b shifter_2__32b_16 (.A(shifter_2__32b_15_s), .S(shifter_2__32b_16_s));
  shifter_2__32b shifter_2__32b_17 (.A(shifter_2__32b_16_s), .S(shifter_2__32b_17_s));
  shifter_2__32b shifter_2__32b_18 (.A(shifter_2__32b_17_s), .S(shifter_2__32b_18_s));
  shifter_2__32b shifter_2__32b_19 (.A(shifter_2__32b_18_s), .S(shifter_2__32b_19_s));
  shifter_2__32b shifter_2__32b_20 (.A(shifter_2__32b_19_s), .S(shifter_2__32b_20_s));
  shifter_2__32b shifter_2__32b_21 (.A(shifter_2__32b_20_s), .S(shifter_2__32b_21_s));
  shifter_2__32b shifter_2__32b_22 (.A(shifter_2__32b_21_s), .S(shifter_2__32b_22_s));
  shifter_2__32b shifter_2__32b_23 (.A(shifter_2__32b_22_s), .S(shifter_2__32b_23_s));
  shifter_2__32b shifter_2__32b_24 (.A(shifter_2__32b_23_s), .S(shifter_2__32b_24_s));
  shifter_2__32b shifter_2__32b_25 (.A(shifter_2__32b_24_s), .S(shifter_2__32b_25_s));
  shifter_2__32b shifter_2__32b_26 (.A(shifter_2__32b_25_s), .S(shifter_2__32b_26_s));
  shifter_2__32b shifter_2__32b_27 (.A(shifter_2__32b_26_s), .S(shifter_2__32b_27_s));
  shifter_2__32b shifter_2__32b_28 (.A(shifter_2__32b_27_s), .S(shifter_2__32b_28_s));
  shifter_2__32b shifter_2__32b_29 (.A(shifter_2__32b_28_s), .S(shifter_2__32b_29_s));
  shifter_2__32b shifter_2__32b_30 (.A(shifter_2__32b_29_s), .S(shifter_2__32b_30_s));
  shifter_2__32b shifter_2__32b_31 (.A(shifter_2__32b_30_s), .S(shifter_2__32b_31_s));
  Multiplexer #(.Selector_Bits(5), .Bits(32)) multiplexer_1 (
    .sel(B[4:0]), .in_0(A), .in_1(shifter_2__32b_1_s), .in_2(shifter_2__32b_2_s), .in_3(shifter_2__32b_3_s),
    .in_4(shifter_2__32b_4_s), .in_5(shifter_2__32b_5_s), .in_6(shifter_2__32b_6_s),
    .in_7(shifter_2__32b_7_s), .in_8(shifter_2__32b_8_s), .in_9(shifter_2__32b_9_s),
    .in_10(shifter_2__32b_10_s), .in_11(shifter_2__32b_11_s), .in_12(shifter_2__32b_12_s),
    .in_13(shifter_2__32b_13_s), .in_14(shifter_2__32b_14_s), .in_15(shifter_2__32b_15_s),
    .in_16(shifter_2__32b_16_s), .in_17(shifter_2__32b_17_s), .in_18(shifter_2__32b_18_s),
    .in_19(shifter_2__32b_19_s), .in_20(shifter_2__32b_20_s), .in_21(shifter_2__32b_21_s),
    .in_22(shifter_2__32b_22_s), .in_23(shifter_2__32b_23_s), .in_24(shifter_2__32b_24_s),
    .in_25(shifter_2__32b_25_s), .in_26(shifter_2__32b_26_s), .in_27(shifter_2__32b_27_s),
    .in_28(shifter_2__32b_28_s), .in_29(shifter_2__32b_29_s), .in_30(shifter_2__32b_30_s),
    .in_31(shifter_2__32b_31_s), .out(S));
endmodule
