// Digital circuit R_Shifter_16b.dig as structural Verilog
module R_Shifter_16b (
  input  Sig,
  input  [15:0] A,
  input  MSB,
  output LSB,
  output [15:0] S
);

  wire r_shifter_4b_1_lsb, r_shifter_4b_2_lsb, r_shifter_4b_3_lsb;

  R_Shifter_4b r_shifter_4b_1 (.MSB(MSB), .A(A[15:12]), .S(S[15:12]), .LSB(r_shifter_4b_1_lsb), .Sig(Sig));
  R_Shifter_4b r_shifter_4b_2 (.MSB(r_shifter_4b_1_lsb), .A(A[11:8]), .S(S[11:8]), .LSB(r_shifter_4b_2_lsb), .Sig(Sig));
  R_Shifter_4b r_shifter_4b_3 (.MSB(r_shifter_4b_2_lsb), .A(A[7:4]), .S(S[7:4]), .LSB(r_shifter_4b_3_lsb), .Sig(Sig));
  R_Shifter_4b r_shifter_4b_4 (.MSB(r_shifter_4b_3_lsb), .A(A[3:0]), .S(S[3:0]), .LSB(LSB), .Sig(Sig));
endmodule
