// Digital circuit Shifter_16bit.dig as structural Verilog
module Shifter_16bit (
  input  Sig,
  input  [15:0] A,
  input  LSB,
  output [15:0] S,
  output MSB
);

  wire shifter_4b_2_msb, shifter_4b_3_msb, shifter_4b_4_msb;

  Shifter_4b shifter_4b_1 (.A(A[15:12]), .LSB(shifter_4b_2_msb), .Sig(Sig), .MSB(MSB), .S(S[15:12]));
  Shifter_4b shifter_4b_2 (.A(A[11:8]), .LSB(shifter_4b_3_msb), .Sig(Sig), .MSB(shifter_4b_2_msb), .S(S[11:8]));
  Shifter_4b shifter_4b_3 (.A(A[7:4]), .LSB(shifter_4b_4_msb), .Sig(Sig), .MSB(shifter_4b_3_msb), .S(S[7:4]));
  Shifter_4b shifter_4b_4 (.A(A[3:0]), .LSB(LSB), .Sig(Sig), .MSB(shifter_4b_4_msb), .S(S[3:0]));
endmodule
