// Digital circuit Somador_Look_Ahead_16bits.dig as structural Verilog
module Somador_Look_Ahead_16bits (
  input  [15:0] A,
  input  [15:0] B,
  input  Cin,
  output Cout,
  output [15:0] S
);

  wire somador_look_ahead_2_c4, somador_look_ahead_3_c4, somador_look_ahead_4_c4;

  Somador_Look_Ahead somador_look_ahead_1 (
    .A(A[15:12]), .B(B[15:12]), .C4(Cout), .S(S[15:12]), .Cin(somador_look_ahead_2_c4));
  Somador_Look_Ahead somador_look_ahead_2 (
    .A(A[11:8]), .B(B[11:8]), .C4(somador_look_ahead_2_c4), .S(S[11:8]), .Cin(somador_look_ahead_3_c4));
  Somador_Look_Ahead somador_look_ahead_3 (
    .A(A[7:4]), .B(B[7:4]), .C4(somador_look_ahead_3_c4), .S(S[7:4]), .Cin(somador_look_ahead_4_c4));
  Somador_Look_Ahead somador_look_ahead_4 (.A(A[3:0]), .B(B[3:0]), .C4(somador_look_ahead_4_c4), .S(S[3:0]), .Cin(Cin));
endmodule
