// Digital circuit Subtrator_Look_Ahead_32_bits.dig as structural Verilog
module Subtrator_Look_Ahead_32_bits (
  input  [31:0] A,
  input  [31:0] B,
  output [31:0] S
);

  wire somador_look_ahead_16bits_2_cout;
  wire [15:0] not_1_out, not_1_out_2;

  Somador_Look_Ahead_16bits somador_look_ahead_16bits_1 (
    .A(A[31:16]), .B(not_1_out_2), .S(S[31:16]), .Cin(somador_look_ahead_16bits_2_cout));  // open: Cout
  assign {not_1_out_2, not_1_out} = ~B;  // Not not_1, 32 bits wide
  Somador_Look_Ahead_16bits somador_look_ahead_16bits_2 (
    .A(A[15:0]), .B(not_1_out), .Cout(somador_look_ahead_16bits_2_cout), .S(S[15:0]), .Cin(1'b1));
endmodule
