// Digital circuit Zero_32.dig as structural Verilog
module Zero_32 (
  input  [31:0] A,
  output ZERO
);

  wire [15:0] not_1_out;
  wire [31:16] not_1_out_2;

  and and_1 (ZERO, not_1_out[15], not_1_out[14], not_1_out[13], not_1_out[12], not_1_out[11], not_1_out[10], not_1_out[9], not_1_out[8], not_1_out[7], not_1_out[6], not_1_out[5], not_1_out[4], not_1_out[3], not_1_out[2], not_1_out[1], not_1_out[0], not_1_out_2[16], not_1_out_2[17], not_1_out_2[18], not_1_out_2[19], not_1_out_2[20], not_1_out_2[21], not_1_out_2[22], not_1_out_2[23], not_1_out_2[24], not_1_out_2[25], not_1_out_2[26], not_1_out_2[27], not_1_out_2[28], not_1_out_2[29], not_1_out_2[30], not_1_out_2[31]);
  assign {not_1_out_2, not_1_out} = ~A;  // Not not_1, 32 bits wide
endmodule
