// Digital circuit shifter(2)_32b.dig as structural Verilog
module shifter_2__32b (
  input  [31:0] A,
  output [31:0] S
);

  wire shifter_16bit_2_msb;

  Shifter_16bit shifter_16bit_1 (.Sig(1'b1), .A(A[31:16]), .LSB(shifter_16bit_2_msb), .S(S[31:16]));  // open: MSB
  Shifter_16bit shifter_16bit_2 (.Sig(1'b1), .A(A[15:0]), .LSB(1'b0), .MSB(shifter_16bit_2_msb), .S(S[15:0]));
endmodule
